// Logisim project Sim-AC-Harvard.circ as structural Verilog: 15 circuits, main circuit Sumador-Restador 4 bits
module Semisumador_1_bit (
  input  A,
  input  B,
  output Resultado,
  output Acarreo_out
);

  and and_1 (Acarreo_out, A, B);
  xor xor_1 (Resultado, A, B);

  // Notes on the sheet:
  //   Semisumador
  //   B
  //   A
  //   0
  //   0
  //   0
  //   1
  //   1
  //   0
  //   1
  //   1
  //   AND
  //   0
  //   0
  //   0
  //   1
  //   B
  //   A
  //   0
  //   0
  //   0
  //   0
  //   0
  //   1
  //   1
  //   0
  //   0
  //   1
  //   1
  //   1
  //   B
  //   A
  //   XOR
  //   0
  //   0
  //   0
  //   0
  //   1
  //   1
  //   1
  //   0
  //   1
  //   1
  //   1
  //   0
  //   Resultado
  //   Acarreo-out
  //   0
  //   1
  //   1
  //   0
  //   = 0
  //   = 1
  //   = 1
  //   = 2
endmodule

module Sumadorcompleto_1_bit (
  input  Acarreo_in,
  input  A,
  input  B,
  output Resultado,
  output Acarreo_out
);

  wire and_1_out, and_2_out, xor_1_out;

  and and_1 (and_1_out, A, B);
  xor xor_1 (xor_1_out, A, B);
  or or_1 (Acarreo_out, and_1_out, and_2_out);
  and and_2 (and_2_out, Acarreo_in, xor_1_out);
  xor xor_2 (Resultado, Acarreo_in, xor_1_out);

  // Notes on the sheet:
  //   Semisumador
  //   Sumador completo
  //   Semisumador
endmodule

module Sumador_Restador_4_bits (
  input  Op,
  input  [3:0] A,
  input  [3:0] B,
  output [3:0] Resultado,
  output Acarreo_out
);

  wire sumadorcompleto_1_bit_1_acarreo_out, sumadorcompleto_1_bit_2_acarreo_out,
       sumadorcompleto_1_bit_3_acarreo_out, xor_1_out, xor_2_out, xor_3_out, xor_4_out;

  // Probe on A
  // Probe on B
  // Probe on A
  // Probe on B
  xor xor_1 (xor_1_out, Op, B[3]);
  xor xor_2 (xor_2_out, Op, B[2]);
  xor xor_3 (xor_3_out, Op, B[1]);
  xor xor_4 (xor_4_out, Op, B[0]);
  Sumadorcompleto_1_bit sumadorcompleto_1_bit_1 (
    .A(A[0]), .B(xor_4_out), .Resultado(Resultado[0]), .Acarreo_out(sumadorcompleto_1_bit_1_acarreo_out),
    .Acarreo_in(Op));
  Sumadorcompleto_1_bit sumadorcompleto_1_bit_2 (
    .A(A[1]), .B(xor_3_out), .Resultado(Resultado[1]), .Acarreo_out(sumadorcompleto_1_bit_2_acarreo_out),
    .Acarreo_in(sumadorcompleto_1_bit_1_acarreo_out));
  Sumadorcompleto_1_bit sumadorcompleto_1_bit_3 (
    .A(A[2]), .B(xor_2_out), .Resultado(Resultado[2]), .Acarreo_out(sumadorcompleto_1_bit_3_acarreo_out),
    .Acarreo_in(sumadorcompleto_1_bit_2_acarreo_out));
  Sumadorcompleto_1_bit sumadorcompleto_1_bit_4 (
    .A(A[3]), .B(xor_1_out), .Resultado(Resultado[3]), .Acarreo_out(Acarreo_out),
    .Acarreo_in(sumadorcompleto_1_bit_3_acarreo_out));
  // Probe on Resultado
  // Probe on Resultado

  // Notes on the sheet:
  //   Acarreo-in
  //   0
  //   1
  //   Op
  //   Sumar
  //   Restar
endmodule

module Sumador_Restador_8_bits (
  input  Op,
  input  [7:0] A,
  input  [7:0] B,
  output [7:0] Resultado,
  output Acarreo_out
);

  wire sumadorcompleto_1_bit_1_acarreo_out, sumadorcompleto_1_bit_2_acarreo_out,
       sumadorcompleto_1_bit_3_acarreo_out, sumadorcompleto_1_bit_4_acarreo_out,
       sumadorcompleto_1_bit_5_acarreo_out, sumadorcompleto_1_bit_6_acarreo_out,
       sumadorcompleto_1_bit_7_acarreo_out, xor_1_out, xor_2_out, xor_3_out, xor_4_out, xor_5_out, xor_6_out,
       xor_7_out, xor_8_out;

  // Probe on A
  // Probe on B
  // Probe on A
  // Probe on B
  xor xor_1 (xor_1_out, Op, B[7]);
  xor xor_2 (xor_2_out, Op, B[6]);
  xor xor_3 (xor_3_out, Op, B[5]);
  xor xor_4 (xor_4_out, Op, B[4]);
  xor xor_5 (xor_5_out, Op, B[3]);
  xor xor_6 (xor_6_out, Op, B[2]);
  xor xor_7 (xor_7_out, Op, B[1]);
  xor xor_8 (xor_8_out, Op, B[0]);
  Sumadorcompleto_1_bit sumadorcompleto_1_bit_1 (
    .A(A[0]), .B(xor_8_out), .Resultado(Resultado[0]), .Acarreo_out(sumadorcompleto_1_bit_1_acarreo_out),
    .Acarreo_in(Op));
  Sumadorcompleto_1_bit sumadorcompleto_1_bit_2 (
    .A(A[1]), .B(xor_7_out), .Resultado(Resultado[1]), .Acarreo_out(sumadorcompleto_1_bit_2_acarreo_out),
    .Acarreo_in(sumadorcompleto_1_bit_1_acarreo_out));
  Sumadorcompleto_1_bit sumadorcompleto_1_bit_3 (
    .A(A[2]), .B(xor_6_out), .Resultado(Resultado[2]), .Acarreo_out(sumadorcompleto_1_bit_3_acarreo_out),
    .Acarreo_in(sumadorcompleto_1_bit_2_acarreo_out));
  Sumadorcompleto_1_bit sumadorcompleto_1_bit_4 (
    .A(A[3]), .B(xor_5_out), .Resultado(Resultado[3]), .Acarreo_out(sumadorcompleto_1_bit_4_acarreo_out),
    .Acarreo_in(sumadorcompleto_1_bit_3_acarreo_out));
  Sumadorcompleto_1_bit sumadorcompleto_1_bit_5 (
    .A(A[4]), .B(xor_4_out), .Resultado(Resultado[4]), .Acarreo_out(sumadorcompleto_1_bit_5_acarreo_out),
    .Acarreo_in(sumadorcompleto_1_bit_4_acarreo_out));
  Sumadorcompleto_1_bit sumadorcompleto_1_bit_6 (
    .A(A[5]), .B(xor_3_out), .Resultado(Resultado[5]), .Acarreo_out(sumadorcompleto_1_bit_6_acarreo_out),
    .Acarreo_in(sumadorcompleto_1_bit_5_acarreo_out));
  Sumadorcompleto_1_bit sumadorcompleto_1_bit_7 (
    .A(A[6]), .B(xor_2_out), .Resultado(Resultado[6]), .Acarreo_out(sumadorcompleto_1_bit_7_acarreo_out),
    .Acarreo_in(sumadorcompleto_1_bit_6_acarreo_out));
  Sumadorcompleto_1_bit sumadorcompleto_1_bit_8 (
    .A(A[7]), .B(xor_1_out), .Resultado(Resultado[7]), .Acarreo_out(Acarreo_out),
    .Acarreo_in(sumadorcompleto_1_bit_7_acarreo_out));
  // Probe on Resultado
  // Probe on Resultado

  // Notes on the sheet:
  //   Acarreo-in
  //   0
  //   1
  //   Op
  //   Sumar
  //   Restar
endmodule

module Sumador_Restador_con_flags (
  input  Op,
  input  [7:0] A,
  input  [7:0] B,
  output Acarreo__Carry,
  output Cero__Zero,
  output [7:0] Resultado
);

  wire A_Out, not_1_out, sumadorcompleto_1_bit_1_acarreo_out, sumadorcompleto_1_bit_2_acarreo_out,
       sumadorcompleto_1_bit_3_acarreo_out, sumadorcompleto_1_bit_4_acarreo_out,
       sumadorcompleto_1_bit_5_acarreo_out, sumadorcompleto_1_bit_6_acarreo_out,
       sumadorcompleto_1_bit_7_acarreo_out, xor_1_out, xor_2_out, xor_3_out, xor_4_out, xor_5_out, xor_6_out,
       xor_7_out, xor_8_out;

  // Probe on A
  // Probe on B
  // Probe on A
  // Probe on B
  xor xor_1 (xor_1_out, Op, B[7]);
  xor xor_2 (xor_2_out, Op, B[6]);
  xor xor_3 (xor_3_out, Op, B[5]);
  xor xor_4 (xor_4_out, Op, B[4]);
  xor xor_5 (xor_5_out, Op, B[3]);
  xor xor_6 (xor_6_out, Op, B[2]);
  xor xor_7 (xor_7_out, Op, B[1]);
  xor xor_8 (xor_8_out, Op, B[0]);
  Sumadorcompleto_1_bit sumadorcompleto_1_bit_1 (
    .A(A[0]), .B(xor_8_out), .Resultado(Resultado[0]), .Acarreo_out(sumadorcompleto_1_bit_1_acarreo_out),
    .Acarreo_in(Op));
  Sumadorcompleto_1_bit sumadorcompleto_1_bit_2 (
    .A(A[1]), .B(xor_7_out), .Resultado(Resultado[1]), .Acarreo_out(sumadorcompleto_1_bit_2_acarreo_out),
    .Acarreo_in(sumadorcompleto_1_bit_1_acarreo_out));
  Sumadorcompleto_1_bit sumadorcompleto_1_bit_3 (
    .A(A[2]), .B(xor_6_out), .Resultado(Resultado[2]), .Acarreo_out(sumadorcompleto_1_bit_3_acarreo_out),
    .Acarreo_in(sumadorcompleto_1_bit_2_acarreo_out));
  Sumadorcompleto_1_bit sumadorcompleto_1_bit_4 (
    .A(A[3]), .B(xor_5_out), .Resultado(Resultado[3]), .Acarreo_out(sumadorcompleto_1_bit_4_acarreo_out),
    .Acarreo_in(sumadorcompleto_1_bit_3_acarreo_out));
  Sumadorcompleto_1_bit sumadorcompleto_1_bit_5 (
    .A(A[4]), .B(xor_4_out), .Resultado(Resultado[4]), .Acarreo_out(sumadorcompleto_1_bit_5_acarreo_out),
    .Acarreo_in(sumadorcompleto_1_bit_4_acarreo_out));
  Sumadorcompleto_1_bit sumadorcompleto_1_bit_6 (
    .A(A[5]), .B(xor_3_out), .Resultado(Resultado[5]), .Acarreo_out(sumadorcompleto_1_bit_6_acarreo_out),
    .Acarreo_in(sumadorcompleto_1_bit_5_acarreo_out));
  Sumadorcompleto_1_bit sumadorcompleto_1_bit_7 (
    .A(A[6]), .B(xor_2_out), .Resultado(Resultado[6]), .Acarreo_out(sumadorcompleto_1_bit_7_acarreo_out),
    .Acarreo_in(sumadorcompleto_1_bit_6_acarreo_out));
  Sumadorcompleto_1_bit sumadorcompleto_1_bit_8 (
    .A(A[7]), .B(xor_1_out), .Resultado(Resultado[7]), .Acarreo_out(A_Out),
    .Acarreo_in(sumadorcompleto_1_bit_7_acarreo_out));
  not not_1 (not_1_out, A_Out);
  nor nor_1 (Cero__Zero, Resultado[0], Resultado[1], Resultado[2], Resultado[3], Resultado[4], Resultado[5], Resultado[6], Resultado[7]);
  // Probe on Resultado
  Multiplexer #(.enable("false")) multiplexer_1 (.in0(A_Out), .in1(not_1_out), .out(Acarreo__Carry), .sel(Op));
  // Probe on Resultado

  // Notes on the sheet:
  //   Acarreo-in
  //   0
  //   1
  //   Op
  //   Sumar
  //   Restar
  //   En la operación restar A+(-B) --> Acarreo =1, si A+(-B) está dentro del rango {0..255}
  //   Se cambia el comportamiento del Acarreo =1 en la operación restar --> Acerreo = 1, si A+(-B) < 0
  //   Para la operación +/- el acarreo = 1, si el resultado cae fuera del rango{0..255}
  //   En la operación sumar A+B --> Acarreo =1 si A+B > 255
  //   {0..255}
  //   Rango de valores enteros representables con 8 bits sin signo
  //   Entonces A<B porque A +(-B) <0 
  //   Funciona así:
  //   Si Acarreo (Carry) = 1:  A >= B
  //   Si Acarreo (Carry) = 0:  A < B 
  //   Pero queremos que funcione así:
  //   Si Acarreo (Carry) = 1:  A < B 
  //   A<B --> C=1
  //   Si Acarreo (Carry) = 0:  A >= B
endmodule

module _1__ALU__ADD_SUB (
  input  Clock,
  input  [7:0] Dato_desde_memoria,
  input  ALUOp
);

  wire [7:0] register_1_q, sumador_restador_8_bits_1_resultado;

  // Probe on sumador_restador_8_bits_1_resultado
  // Probe on sumador_restador_8_bits_1_resultado
  Register register_1 (.D(sumador_restador_8_bits_1_resultado), .Q(register_1_q), .clk(Clock));  // open: en, clr
  // Probe on sumador_restador_8_bits_1_resultado
  // Probe on register_1_q
  // Probe on register_1_q
  // Probe on register_1_q
  // Probe on Dato_desde_memoria
  // Probe on Dato_desde_memoria
  // Probe on Dato_desde_memoria
  Sumador_Restador_8_bits sumador_restador_8_bits_1 (
    .Op(ALUOp), .A(register_1_q), .B(Dato_desde_memoria), .Resultado(sumador_restador_8_bits_1_resultado));  // open: Acarreo_out

  // Notes on the sheet:
  //   Set de instrucciones
  //   Operaciones
  //   ADD
  //   SUB
  //   CodeOp
  //   0
  //   0
  //   0 =
  //   1 =
  //   1
  //   1
  //   ALUOp
  //   1. ALU (ADD-SUB)
  //   Registro
  //   Registro AC: ACumulador
  //   AC
  //   ALUOp
  //   AC: registro ACumulador se escribe por flanco ascendente o de subida, es decir cuando cambia de 0 a 1 el clock
endmodule

module _2__Cargar_de_memoria__LDA (
  input  Clock,
  input  [4:0] \Dirección 
);

  wire [7:0] multiplexer_1_out, ram_1_data, ram_2_data, register_1_q, sumador_restador_8_bits_1_resultado;

  // Probe on \Dirección 
  // Probe on \Dirección 
  RAM #(.addrWidth(5)) ram_1 (.addr(\Dirección ), .data(ram_1_data));  // open: sel, clk, ld, clr
  // Probe on ram_1_data[4:0]
  // Probe on ram_1_data[4:0]
  // Probe on ram_1_data[7:5]
  // Probe on ram_1_data[7:5]
  Register register_1 (.D(sumador_restador_8_bits_1_resultado), .Q(register_1_q), .clk(Clock));  // open: en, clr
  Multiplexer #(.width(8), .enable("false")) multiplexer_1 (
    .in0(register_1_q), .in1({8{1'b0}}), .out(multiplexer_1_out), .sel(ram_1_data[6]));
  // Probe on sumador_restador_8_bits_1_resultado
  // Probe on sumador_restador_8_bits_1_resultado
  // Probe on sumador_restador_8_bits_1_resultado
  // Probe on multiplexer_1_out
  // Probe on multiplexer_1_out
  // Probe on multiplexer_1_out
  // Probe on ram_2_data
  // Probe on ram_2_data
  // Probe on ram_2_data
  Sumador_Restador_8_bits sumador_restador_8_bits_1 (
    .Op(ram_1_data[5]), .A(multiplexer_1_out), .B(ram_2_data), .Resultado(sumador_restador_8_bits_1_resultado));  // open: Acarreo_out
  RAM #(.addrWidth(5), .bus("separate")) ram_2 (
    .addr(ram_1_data[4:0]), .data(ram_2_data));  // open: din, str, sel, clk, ld, clr

  // Notes on the sheet:
  //   Set de instrucciones
  //   Sintaxis
  //   ADD [dirección]
  //   SUB [dirección]
  //   LDA [dirección]
  //   La [dirección] es una posición de la memoria de datos
  //   LDA [dirección] = LOAD ACCUMULATOR
  //   CodeOp
  //   000
  //   0 =
  //   1 =
  //   001
  //   2 =
  //   010
  //   2. Cargar de memoria (LDA)
  //   Señales de control
  //   AluX
  //   ALUOp
  //   0
  //   0
  //   0
  //   1
  //   1
  //   0
  //   0
  //   1
  //   2
  //   3
  //   Memoria de instrucciones
  //   Código.mem
  //   LDA [0]
  //   ADD [1]
  //   LDA [2]
  //   SUB [3]
  //    = 0x40 hex
  //    = 0x01 hex
  //    = 0x42 hex
  //    = 0x23 hex
  //   Formato Instrucción
  //   CodeOp
  //   | b7 b6  b5 | b4 b3 b2 b1 b0 | 
  //   Dirección
  //   CodeOp
  //   (byte 1)
  //   Dirección
  //   AC
  //   !!Cantidad de posiciones direccionables 2**5 = 32 posiciones
  //   AluX
  //   ALUOp
  //   Arquitectura Harvard
  //   Memoria de datos e intrucciones separadas
  //   datos.mem
  //   0x02 hex
  //   0
  //   0x03 hex
  //   1
  //   0x04 hex
  //   2
  //   0x01 hex
  //   3
  //   Memoria de datos
endmodule

module _3__Registro_Program_Counter__PC (
  input  Clock
);

  wire [4:0] adder_1_out, register_1_q;
  wire [7:0] multiplexer_1_out, ram_1_data, ram_2_data, register_2_q, sumador_restador_8_bits_1_resultado;

  Adder #(.width(5)) adder_1 (.a(register_1_q), .b(5'b00001), .out(adder_1_out));  // open: cin, cout
  // Probe on register_1_q
  // Probe on adder_1_out
  Register #(.width(5)) register_1 (.D(adder_1_out), .Q(register_1_q), .clk(Clock));  // open: en, clr
  // Probe on register_1_q
  // Probe on register_1_q
  RAM #(.addrWidth(5)) ram_1 (.addr(register_1_q), .data(ram_1_data));  // open: sel, clk, ld, clr
  // Probe on ram_1_data[4:0]
  // Probe on ram_1_data[4:0]
  // Probe on ram_1_data[7:5]
  // Probe on ram_1_data[7:5]
  Register register_2 (.D(sumador_restador_8_bits_1_resultado), .Q(register_2_q), .clk(Clock));  // open: en, clr
  // Probe on sumador_restador_8_bits_1_resultado
  // Probe on sumador_restador_8_bits_1_resultado
  // Probe on sumador_restador_8_bits_1_resultado
  Multiplexer #(.width(8), .enable("false")) multiplexer_1 (
    .in0(register_2_q), .in1({8{1'b0}}), .out(multiplexer_1_out), .sel(ram_1_data[6]));
  // Probe on multiplexer_1_out
  // Probe on multiplexer_1_out
  // Probe on multiplexer_1_out
  // Probe on ram_2_data
  // Probe on ram_2_data
  // Probe on ram_2_data
  Sumador_Restador_8_bits sumador_restador_8_bits_1 (
    .Op(ram_1_data[5]), .A(multiplexer_1_out), .B(ram_2_data), .Resultado(sumador_restador_8_bits_1_resultado));  // open: Acarreo_out
  RAM #(.addrWidth(5), .bus("separate")) ram_2 (
    .addr(ram_1_data[4:0]), .data(ram_2_data));  // open: din, str, sel, clk, ld, clr

  // Notes on the sheet:
  //   Sintaxis
  //   Registro PC =
  //   Set de instrucciones
  //   ADD [dirección]
  //   SUB [dirección]
  //   LDA [dirección]
  //   Program Counter
  //    PC + 1
  //   0 =
  //   1 =
  //   2 =
  //    El registro PC  se escribe por flanco ascendente o de subida (rising edge)
  //   PC
  //   CodeOp
  //   000
  //   001
  //   010
  //   3. Registro Program Counter (PC)
  //   Señales de control
  //   AluX
  //   ALUOp
  //   0
  //   0
  //   0
  //   1
  //   1
  //   0
  //   LDA [0]
  //   0
  //   ADD [1]
  //   1
  //   LDA [2]
  //   2
  //   SUB [3]
  //   3
  //   Memoria de instrucciones
  //   Código.mem
  //    = 0x40 hex
  //    = 0x01 hex
  //    = 0x42 hex
  //    = 0x23 hex
  //   CodeOp
  //   Formato Instrucción
  //   Dirección
  //   | b7 b6  b5 | b4 b3 b2 b1 b0 | 
  //   AC
  //   Dirección
  //   CodeOp
  //   (byte 1)
  //   AluX
  //   ALUOp
  //   0
  //   1
  //   2
  //   3
  //   datos.mem
  //   0x02 hex
  //   0x03 hex
  //   0x04 hex
  //   0x01 hex
  //   Memoria de datos
endmodule

module _4_1__Almacenar_en_memoria__STA (
  input  Clock
);

  wire AluOp, AluX, AluY, decoder_1_out0, Reset, WriteR;
  wire [4:0] adder_1_out, register_1_q;
  wire [7:0] multiplexer_1_out, multiplexer_2_out, ram_1_data, ram_2_data, register_2_q,
       sumador_restador_8_bits_1_resultado;

  Button u_Reset (.out(Reset));
  Adder #(.width(5)) adder_1 (.a(register_1_q), .b(5'b00001), .out(adder_1_out));  // open: cin, cout
  // Probe on register_1_q
  // Probe on adder_1_out
  Register #(.width(5)) register_1 (.D(adder_1_out), .Q(register_1_q), .clk(Clock), .clr(Reset));  // open: en
  // Probe on register_1_q
  // Probe on register_1_q
  RAM #(.addrWidth(5)) ram_1 (.addr(register_1_q), .data(ram_1_data));  // open: sel, clk, ld, clr
  // Probe on ram_1_data[4:0]
  // Probe on ram_1_data[4:0]
  // Probe on ram_1_data[7:5]
  // Probe on ram_1_data[7:5]
  Decoder #(.select(3), .enable("false")) decoder_1 (
    .out0(decoder_1_out0), .out1(AluOp), .out2(AluX), .out3(AluY), .sel(ram_1_data[7:5]));  // open: out4, out5, out6, out7
  Register register_2 (
    .D(sumador_restador_8_bits_1_resultado), .en(WriteR), .Q(register_2_q), .clk(Clock), .clr(Reset));
  // Probe on sumador_restador_8_bits_1_resultado
  // Probe on sumador_restador_8_bits_1_resultado
  // Probe on sumador_restador_8_bits_1_resultado
  Multiplexer #(.width(8), .enable("false")) multiplexer_1 (
    .in0(register_2_q), .in1({8{1'b0}}), .out(multiplexer_1_out), .sel(AluX));
  Multiplexer #(.width(8), .enable("false")) multiplexer_2 (
    .in0(ram_2_data), .in1({8{1'b0}}), .out(multiplexer_2_out), .sel(AluY));
  or or_1 (WriteR, decoder_1_out0, AluOp, AluX);
  // Probe on multiplexer_1_out
  // Probe on multiplexer_1_out
  // Probe on multiplexer_1_out
  // Probe on multiplexer_2_out
  // Probe on multiplexer_2_out
  // Probe on multiplexer_2_out
  Sumador_Restador_8_bits sumador_restador_8_bits_1 (
    .Op(AluOp), .A(multiplexer_1_out), .B(multiplexer_2_out), .Resultado(sumador_restador_8_bits_1_resultado));  // open: Acarreo_out
  RAM #(.addrWidth(5), .bus("separate")) ram_2 (
    .addr(ram_1_data[4:0]), .din(sumador_restador_8_bits_1_resultado), .data(ram_2_data), .str(AluY),
    .clk(Clock));  // open: sel, ld, clr

  // Other names for the same wires on the sheet: WriteMD = AluY

  // Notes on the sheet:
  //   Sintaxis
  //   Set de instrucciones
  //   ADD [dirección]
  //   SUB [dirección]
  //   LDA [dirección]
  //   STA [dirección]
  //    PC + 1
  //   CodeOp
  //   0 =
  //   1 =
  //   2 =
  //   3 =
  //   STA [dirección] = STORE ACCUMULATOR
  //   PC
  //   AluX
  //   0
  //   000
  //   0
  //   001
  //   1
  //   010
  //   0
  //   011
  //   4.1. Almacenar en memoria (STA)
  //   ALUOp
  //   AluY
  //   0
  //   0
  //   0
  //   0
  //   1
  //   0
  //   0
  //   1
  //   2
  //   Señales de control
  //   WriteR
  //   0
  //   1
  //   1
  //   1
  //   1
  //   0
  //   Memoria de instrucciones
  //   Código.mem
  //   LDA [0]
  //   ADD [1]
  //   STA [2]
  //   WriteMD
  //   0
  //   0
  //   0
  //   1
  //    = 0x40 hex
  //    = 0x01 hex
  //    = 0x62 hex
  //   Dirección
  //   CodeOp
  //   Formato Instrucción
  //   CodeOp
  //   | b7 b6  b5 | b4 b3 b2 b1 b0 | 
  //   Dirección
  //   AC
  //   Unidad de Control
  //   (byte 1)
  //    Habilitación escritura registro AC
  //    Habilitación escritura Memoria de Datos
  //   0
  //   1
  //   La memoria se escibe por flanco ascendente o de subida (Rising edge)
  //   datos.mem
  //   0x02 hex
  //   0x03 hex
  //   Memoria de datos
endmodule

module _4_2__Almacenar_en_memoria__STA (
  input  Clock
);

  wire AluOp, AluX, AluY, decoder_1_out0, Reset, WriteR;
  wire [4:0] counter_1_q;
  wire [7:0] multiplexer_1_out, multiplexer_2_out, ram_1_data, ram_2_data, register_1_q,
       sumador_restador_8_bits_1_resultado;

  Button u_Reset (.out(Reset));
  Counter #(.width(5), .max('h1f)) counter_1 (
    .count(1'b1), .Q(counter_1_q), .clk(Clock), .clr(Reset));  // open: load, D, carry
  // Probe on counter_1_q
  // Probe on counter_1_q
  RAM #(.addrWidth(5)) ram_1 (.addr(counter_1_q), .data(ram_1_data));  // open: sel, clk, ld, clr
  // Probe on ram_1_data[4:0]
  // Probe on ram_1_data[4:0]
  // Probe on ram_1_data[7:5]
  // Probe on ram_1_data[7:5]
  Decoder #(.select(3), .enable("false")) decoder_1 (
    .out0(decoder_1_out0), .out1(AluOp), .out2(AluX), .out3(AluY), .sel(ram_1_data[7:5]));  // open: out4, out5, out6, out7
  Register register_1 (
    .D(sumador_restador_8_bits_1_resultado), .en(WriteR), .Q(register_1_q), .clk(Clock), .clr(Reset));
  or or_1 (WriteR, decoder_1_out0, AluOp, AluX);
  // Probe on sumador_restador_8_bits_1_resultado
  // Probe on sumador_restador_8_bits_1_resultado
  // Probe on sumador_restador_8_bits_1_resultado
  Multiplexer #(.width(8), .enable("false")) multiplexer_1 (
    .in0(register_1_q), .in1({8{1'b0}}), .out(multiplexer_1_out), .sel(AluX));
  Multiplexer #(.width(8), .enable("false")) multiplexer_2 (
    .in0(ram_2_data), .in1({8{1'b0}}), .out(multiplexer_2_out), .sel(AluY));
  // Probe on multiplexer_1_out
  // Probe on multiplexer_1_out
  // Probe on multiplexer_1_out
  // Probe on multiplexer_2_out
  // Probe on multiplexer_2_out
  // Probe on multiplexer_2_out
  Sumador_Restador_8_bits sumador_restador_8_bits_1 (
    .Op(AluOp), .A(multiplexer_1_out), .B(multiplexer_2_out), .Resultado(sumador_restador_8_bits_1_resultado));  // open: Acarreo_out
  RAM #(.addrWidth(5), .bus("separate")) ram_2 (
    .addr(ram_1_data[4:0]), .din(sumador_restador_8_bits_1_resultado), .data(ram_2_data), .str(AluY),
    .clk(Clock));  // open: sel, ld, clr

  // Other names for the same wires on the sheet: WriteMD = AluY

  // Notes on the sheet:
  //   PC =  PC + 1
  //   Tipo
  //   Procesamiento de datos
  //   Transferencia
  //   Si ct =1 y clock = 1 --> PC =  PC + 1
  //   PC
  //   Set de instrucciones
  //   !!Se organiza las instrucciones por tipo
  //   Sintaxis
  //   ADD [dirección]
  //   SUB [dirección]
  //   LDA [dirección]
  //   STA [dirección]
  //   Código.mem
  //   LDA [0]
  //   0
  //   ADD [1]
  //   1
  //   STA [2]
  //   2
  //   4.2. Almacenar en memoria (STA)
  //   Memoria de instrucciones
  //    = 0x40 hex
  //    = 0x01 hex
  //    = 0x62 hex
  //   CodeOp
  //   000
  //   0 =
  //   001
  //   1 =
  //   2 =
  //   010
  //   3 =
  //   011
  //   CodeOp
  //   AluX
  //   AluY
  //   0
  //   0
  //   0
  //   0
  //   1
  //   0
  //   0
  //   1
  //   Dirección
  //   Señales de control
  //   ALUOp
  //   0
  //   1
  //   0
  //   0
  //   AC
  //   WriteMD
  //   WriteR
  //   1
  //   0
  //   1
  //   0
  //   1
  //   0
  //   0
  //   1
  //   Unidad de Control
  //   CodeOp
  //    Habilitación escritura registro AC
  //   Formato Instrucción
  //   Dirección
  //   | b7 b6  b5 | b4 b3 b2 b1 b0 | 
  //    Habilitación escritura Memoria de Datos
  //   (byte 1)
  //   datos.mem
  //   0
  //   1
  //   Memoria de datos
  //   0x02 hex
  //   0x03 hex
endmodule

module _5__Salto_incondiconal__JMP (
  input  Clock
);

  wire AluOp, AluX, AluY, Contar, decoder_1_out0, JMP, Reset, WriteR;
  wire [4:0] counter_1_q;
  wire [7:0] multiplexer_1_out, multiplexer_2_out, ram_1_data, ram_2_data, register_1_q,
       sumador_restador_8_bits_1_resultado;

  Counter #(.width(5), .max('h1f)) counter_1 (
    .load(JMP), .D(ram_1_data[4:0]), .count(Contar), .Q(counter_1_q), .clk(Clock), .clr(Reset));  // open: carry
  nand nand_1 (Contar, JMP, 1'b1);
  Button u_Reset (.out(Reset));
  // Probe on counter_1_q
  // Probe on counter_1_q
  RAM #(.addrWidth(5)) ram_1 (.addr(counter_1_q), .data(ram_1_data));  // open: sel, clk, ld, clr
  // Probe on ram_1_data[4:0]
  // Probe on ram_1_data[4:0]
  // Probe on ram_1_data[7:5]
  // Probe on ram_1_data[7:5]
  Decoder #(.select(3), .enable("false")) decoder_1 (
    .out0(decoder_1_out0), .out1(AluOp), .out2(AluX), .out3(AluY), .out4(JMP), .sel(ram_1_data[7:5]));  // open: out5, out6, out7
  Register register_1 (
    .D(sumador_restador_8_bits_1_resultado), .en(WriteR), .Q(register_1_q), .clk(Clock), .clr(Reset));
  Multiplexer #(.width(8), .enable("false")) multiplexer_1 (
    .in0(register_1_q), .in1({8{1'b0}}), .out(multiplexer_1_out), .sel(AluX));
  Multiplexer #(.width(8), .enable("false")) multiplexer_2 (
    .in0(ram_2_data), .in1({8{1'b0}}), .out(multiplexer_2_out), .sel(AluY));
  or or_1 (WriteR, decoder_1_out0, AluOp, AluX);
  // Probe on multiplexer_1_out
  // Probe on multiplexer_1_out
  // Probe on multiplexer_1_out
  // Probe on multiplexer_2_out
  // Probe on multiplexer_2_out
  // Probe on multiplexer_2_out
  // Probe on sumador_restador_8_bits_1_resultado
  // Probe on sumador_restador_8_bits_1_resultado
  // Probe on sumador_restador_8_bits_1_resultado
  Sumador_Restador_8_bits sumador_restador_8_bits_1 (
    .Op(AluOp), .A(multiplexer_1_out), .B(multiplexer_2_out), .Resultado(sumador_restador_8_bits_1_resultado));  // open: Acarreo_out
  RAM #(.addrWidth(5), .bus("separate")) ram_2 (
    .addr(ram_1_data[4:0]), .din(sumador_restador_8_bits_1_resultado), .data(ram_2_data), .str(AluY),
    .clk(Clock));  // open: sel, ld, clr

  // Other names for the same wires on the sheet: WriteMD = AluY

  // Notes on the sheet:
  //   Tipo
  //   Procesamiento de datos
  //   Transferencia
  //   Control de flujo
  //   PC =  PC + 1
  //   Set de instrucciones
  //   Load
  //   No incrementa en contador de programa si se produce un salto
  //   Sintaxis
  //   ADD [dirección]
  //   SUB [dirección]
  //   LDA [dirección]
  //   STA [dirección]
  //   JMP dirección
  //   PC
  //   En las instrucciones de control de flujo la [dirección] es una posición de la memoria de instrucciones
  //   0
  //   1
  //   6.1. Saltos condicionales (JZ)
  //   CodeOp
  //   000
  //   0 =
  //   001
  //   1 =
  //   2 =
  //   010
  //   3 =
  //   011
  //   4 =
  //   100
  //   Memoria de instrucciones
  //   Código.mem
  //   LDA [0]
  //   JMP 3
  //   STA [2]
  //   2
  //   JMP 0
  //   3
  //   AluX
  //   0
  //   0
  //   1
  //   0
  //   0
  //    = 0x40 hex
  //    = 0x83 hex
  //    = 0x62 hex
  //    = 0x80 hex
  //   ALUOp
  //   AluY
  //   0
  //   0
  //   0
  //   1
  //   0
  //   0
  //   1
  //   0
  //   0
  //   0
  //   Dirección
  //   CodeOp
  //   Señales de control
  //   WriteR
  //   WriteMD
  //   1
  //   0
  //   1
  //   0
  //   1
  //   0
  //   0
  //   1
  //   0
  //   0
  //   JMP
  //   0
  //   0
  //   0
  //   0
  //   1
  //   AC
  //   Unidad de Control
  //   Formato Instrucción
  //   CodeOp
  //   Dirección
  //   | b7 b6 b5 | b4 b3 b2 b1 b0 | 
  //    Habilitación escritura registro AC
  //    Habilitación escritura Memoria de Datos
  //   (byte 1)
  //   datos.mem
  //   0x02 hex
  //   0
  //   0x03 hex
  //   1
  //   Memoria de datos
endmodule

module _6_1__Saltos_condicionales__JZ (
  input  Clock
);

  wire AluOp, AluX, AluY, and_1_out, Contar, decoder_1_out0, decoder_1_out4, decoder_1_out5, FZ, JMP, Reset,
       WriteF, WriteR, Z;
  wire [4:0] counter_1_q;
  wire [7:0] multiplexer_1_out, multiplexer_2_out, ram_1_data, ram_2_data, register_2_q,
       sumador_restador_con_flags_1_resultado;

  Button u_Reset (.out(Reset));
  Counter #(.width(5), .max('h1f)) counter_1 (
    .load(JMP), .D(ram_1_data[4:0]), .count(Contar), .Q(counter_1_q), .clk(Clock), .clr(Reset));  // open: carry
  nand nand_1 (Contar, JMP, 1'b1);
  // Probe on counter_1_q
  // Probe on counter_1_q
  RAM #(.addrWidth(5)) ram_1 (.addr(counter_1_q), .data(ram_1_data));  // open: sel, clk, ld, clr
  // Probe on ram_1_data[4:0]
  // Probe on ram_1_data[4:0]
  // Probe on ram_1_data[7:5]
  // Probe on ram_1_data[7:5]
  Register #(.width(1)) register_1 (.D(Z), .en(WriteF), .Q(FZ), .clk(Clock), .clr(Reset));
  Decoder #(.select(3), .enable("false")) decoder_1 (
    .out0(decoder_1_out0), .out1(AluOp), .out2(AluX), .out3(AluY), .out4(decoder_1_out4),
    .out5(decoder_1_out5), .sel(ram_1_data[7:5]));  // open: out6, out7
  Register register_2 (
    .D(sumador_restador_con_flags_1_resultado), .en(WriteR), .Q(register_2_q), .clk(Clock), .clr(Reset));
  Multiplexer #(.width(8), .enable("false")) multiplexer_1 (
    .in0(register_2_q), .in1({8{1'b0}}), .out(multiplexer_1_out), .sel(AluX));
  Multiplexer #(.width(8), .enable("false")) multiplexer_2 (
    .in0(ram_2_data), .in1({8{1'b0}}), .out(multiplexer_2_out), .sel(AluY));
  or or_1 (WriteR, decoder_1_out0, AluOp, AluX);
  or or_2 (WriteF, decoder_1_out0, AluOp);
  or or_3 (JMP, decoder_1_out4, and_1_out);
  and and_1 (and_1_out, decoder_1_out5, FZ);
  // Probe on multiplexer_1_out
  // Probe on multiplexer_1_out
  // Probe on multiplexer_1_out
  // Probe on multiplexer_2_out
  // Probe on multiplexer_2_out
  // Probe on multiplexer_2_out
  // Probe on sumador_restador_con_flags_1_resultado
  // Probe on sumador_restador_con_flags_1_resultado
  // Probe on sumador_restador_con_flags_1_resultado
  Sumador_Restador_con_flags sumador_restador_con_flags_1 (
    .Op(AluOp), .A(multiplexer_1_out), .B(multiplexer_2_out), .Cero__Zero(Z),
    .Resultado(sumador_restador_con_flags_1_resultado));  // open: Acarreo__Carry
  RAM #(.addrWidth(5), .bus("separate")) ram_2 (
    .addr(ram_1_data[4:0]), .din(sumador_restador_con_flags_1_resultado), .data(ram_2_data), .str(AluY),
    .clk(Clock));  // open: sel, ld, clr

  // Other names for the same wires on the sheet: WriteMD = AluY

  // Notes on the sheet:
  //   Tipo
  //   Procesamiento de datos
  //   Transferencia
  //   Control de flujo
  //   PC =  PC + 1
  //   Set de instrucciones
  //   Load
  //   Sintaxis
  //   ADD [dirección]
  //   SUB [dirección]
  //   LDA [dirección]
  //   STA [dirección]
  //   JMP dirección
  //   JZ    dirección
  //   La instrucción JZ salta si el registro Z tiene valor 1
  //   PC
  //   6.1. Saltos condicionales (JZ)
  //   CodeOp
  //   000
  //   0 =
  //   001
  //   1 =
  //   2 =
  //   010
  //   3 =
  //   011
  //   4 =
  //   100
  //   5 =
  //   101
  //   Memoria de instrucciones
  //   Código.mem
  //   LDA [0]
  //   0
  //   SUB [1]
  //   1
  //   JZ 0
  //   2
  //   JMP 0
  //   3
  //   AluX
  //   0
  //   0
  //   1
  //   0
  //   0
  //   0
  //    = 0x40 hex
  //    = 0x21 hex
  //    = 0xA0 hex
  //    = 0x80 hex
  //   ALUOp
  //   AluY
  //   0
  //   0
  //   1
  //   0
  //   0
  //   0
  //   0
  //   1
  //   0
  //   0
  //   0
  //   0
  //   Z
  //   Dirección
  //   CodeOp
  //   Señales de control
  //   WriteR
  //   WriteMD
  //   1
  //   0
  //   1
  //   0
  //   1
  //   0
  //   0
  //   1
  //   0
  //   0
  //   0
  //   0
  //   JMP
  //   0
  //   0
  //   0
  //   0
  //   1
  //   1
  //   WriteF
  //   1
  //   1
  //   0
  //   0
  //   0
  //   0
  //   AC
  //   Unidad de Control
  //   Formato Instrucción
  //   CodeOp
  //    Habilitación escritura registro AC
  //    Habilitación escritura registro Z
  //    Habilitación escritura Memoria de Datos
  //   Dirección
  //   | b7 b6 b5 | b4 b3 b2 b1 b0 | 
  //   Solo para las instrucciones de procesamiento de datos se escribe los registros Flags
  //   (byte 1)
  //   datos.mem
  //   0x02 hex
  //   0
  //   0x02 hex
  //   1
  //   Memoria de datos
endmodule

module _6_2__Saltos_condicionales__JC (
  input  Clock
);

  wire AluOp, AluX, AluY, and_1_out, and_2_out, C, Contar, decoder_1_out0, decoder_1_out4, decoder_1_out5,
       decoder_1_out6, FC, FZ, JMP, Reset, WriteF, WriteR, Z;
  wire [4:0] counter_1_q;
  wire [7:0] multiplexer_1_out, multiplexer_2_out, ram_1_data, ram_2_data, register_3_q,
       sumador_restador_con_flags_1_resultado;

  Button u_Reset (.out(Reset));
  Counter #(.width(5), .max('h1f)) counter_1 (
    .load(JMP), .D(ram_1_data[4:0]), .count(Contar), .Q(counter_1_q), .clk(Clock), .clr(Reset));  // open: carry
  nand nand_1 (Contar, JMP, 1'b1);
  // Probe on counter_1_q
  // Probe on counter_1_q
  Register #(.width(1)) register_1 (.D(Z), .en(WriteF), .Q(FZ), .clk(Clock), .clr(Reset));
  RAM #(.addrWidth(5)) ram_1 (.addr(counter_1_q), .data(ram_1_data));  // open: sel, clk, ld, clr
  Register #(.width(1)) register_2 (.D(C), .en(WriteF), .Q(FC), .clk(Clock), .clr(Reset));
  // Probe on ram_1_data[4:0]
  // Probe on ram_1_data[4:0]
  // Probe on ram_1_data[7:5]
  // Probe on ram_1_data[7:5]
  Decoder #(.select(3), .enable("false")) decoder_1 (
    .out0(decoder_1_out0), .out1(AluOp), .out2(AluX), .out3(AluY), .out4(decoder_1_out4),
    .out5(decoder_1_out5), .out6(decoder_1_out6), .sel(ram_1_data[7:5]));  // open: out7
  Register register_3 (
    .D(sumador_restador_con_flags_1_resultado), .en(WriteR), .Q(register_3_q), .clk(Clock), .clr(Reset));
  Multiplexer #(.width(8), .enable("false")) multiplexer_1 (
    .in0(register_3_q), .in1({8{1'b0}}), .out(multiplexer_1_out), .sel(AluX));
  Multiplexer #(.width(8), .enable("false")) multiplexer_2 (
    .in0(ram_2_data), .in1({8{1'b0}}), .out(multiplexer_2_out), .sel(AluY));
  or or_1 (WriteR, decoder_1_out0, AluOp, AluX);
  or or_2 (WriteF, decoder_1_out0, AluOp);
  and and_1 (and_1_out, decoder_1_out5, FZ);
  and and_2 (and_2_out, decoder_1_out6, FC);
  // Probe on multiplexer_1_out
  // Probe on multiplexer_1_out
  // Probe on multiplexer_1_out
  // Probe on multiplexer_2_out
  // Probe on multiplexer_2_out
  // Probe on multiplexer_2_out
  or or_3 (JMP, decoder_1_out4, and_1_out, and_2_out);
  // Probe on sumador_restador_con_flags_1_resultado
  // Probe on sumador_restador_con_flags_1_resultado
  // Probe on sumador_restador_con_flags_1_resultado
  Sumador_Restador_con_flags sumador_restador_con_flags_1 (
    .Op(AluOp), .A(multiplexer_1_out), .B(multiplexer_2_out), .Acarreo__Carry(C), .Cero__Zero(Z),
    .Resultado(sumador_restador_con_flags_1_resultado));
  RAM #(.addrWidth(5), .bus("separate")) ram_2 (
    .addr(ram_1_data[4:0]), .din(sumador_restador_con_flags_1_resultado), .data(ram_2_data), .str(AluY),
    .clk(Clock));  // open: sel, ld, clr

  // Other names for the same wires on the sheet: WriteMD = AluY

  // Notes on the sheet:
  //   Tipo
  //   Procesamiento de datos
  //   Transferencia
  //   Control de flujo
  //   PC =  PC + 1
  //   Set de instrucciones
  //   Load
  //   Sintaxis
  //   ADD [dirección]
  //   SUB [dirección]
  //   LDA [dirección]
  //   STA [dirección]
  //   JMP dirección
  //   JZ    dirección
  //   JC   dirección
  //   La instrucción JC salta si el registro C tiene valor 1 
  //   PC
  //   0
  //   1
  //   2
  //   3
  //   6.2. Saltos condicionales (JC)
  //   CodeOp
  //   000
  //   0 =
  //   001
  //   1 =
  //   2 =
  //   010
  //   3 =
  //   011
  //   4 =
  //   100
  //   5 =
  //   101
  //   6 =
  //   110
  //   Memoria de instrucciones
  //   Código.mem
  //   LDA [0]
  //   SUB [1]
  //   JC 0
  //   JMP 0
  //   AluX
  //   0
  //   0
  //   1
  //   0
  //   0
  //   0
  //   0
  //   Z
  //    = 0x40 hex
  //    = 0x21 hex
  //    = 0xC0 hex
  //    = 0x80 hex
  //   ALUOp
  //   AluY
  //   0
  //   0
  //   1
  //   0
  //   0
  //   0
  //   1
  //   0
  //   0
  //   0
  //   0
  //   0
  //   0
  //   0
  //   C
  //   Dirección
  //   CodeOp
  //   Señales de control
  //   WriteMD
  //   WriteR
  //   1
  //   0
  //   1
  //   0
  //   1
  //   0
  //   0
  //   1
  //   0
  //   0
  //   0
  //   0
  //   0
  //   0
  //   JMP
  //   0
  //   0
  //   0
  //   0
  //   1
  //   1
  //   1
  //   WriteF
  //   1
  //   1
  //   0
  //   0
  //   0
  //   0
  //   0
  //   AC
  //   Unidad de Control
  //   Formato Instrucción
  //   CodeOp
  //   | b7 b6 b5 | b4 b3 b2 b1 b0 | 
  //    Habilitación escritura registro AC
  //    Habilitación escritura registros Z y C
  //    Habilitación escritura Memoria de Datos
  //   (byte 1)
  //   Dirección
  //   datos.mem
  //   0x02 hex
  //   0
  //   0x03 hex
  //   1
  //   Memoria de datos
endmodule

module _7__Detiene_CPU__HLT (
  input  Clock
);

  wire AluOp, AluX, AluY, and_2_out, and_3_out, C, Clock_PC, Contar, decoder_1_out0, decoder_1_out4,
       decoder_1_out5, decoder_1_out6, FC, FZ, HLT, JMP, Reset, WriteF, WriteR, Z;
  wire [4:0] counter_1_q;
  wire [7:0] multiplexer_1_out, multiplexer_2_out, ram_1_data, ram_2_data, register_3_q,
       sumador_restador_con_flags_1_resultado;

  Button u_Reset (.out(Reset));
  Counter #(.width(5), .max('h1f)) counter_1 (
    .load(JMP), .D(ram_1_data[4:0]), .count(Contar), .Q(counter_1_q), .clk(Clock_PC), .clr(Reset));  // open: carry
  nand nand_1 (Contar, JMP, 1'b1);
  and and_1 (Clock_PC, ~HLT, Clock);  // AND_Gate
  // Probe on counter_1_q
  // Probe on counter_1_q
  Register #(.width(1)) register_1 (.D(Z), .en(WriteF), .Q(FZ), .clk(Clock));  // open: clr
  RAM #(.addrWidth(5)) ram_1 (.addr(counter_1_q), .data(ram_1_data));  // open: sel, clk, ld, clr
  // Probe on ram_1_data[4:0]
  // Probe on ram_1_data[4:0]
  // Probe on ram_1_data[7:5]
  // Probe on ram_1_data[7:5]
  Register #(.width(1)) register_2 (.D(C), .en(WriteF), .Q(FC), .clk(Clock));  // open: clr
  Decoder #(.select(3), .enable("false")) decoder_1 (
    .out0(decoder_1_out0), .out1(AluOp), .out2(AluX), .out3(AluY), .out4(decoder_1_out4),
    .out5(decoder_1_out5), .out6(decoder_1_out6), .out7(HLT), .sel(ram_1_data[7:5]));
  Register register_3 (
    .D(sumador_restador_con_flags_1_resultado), .en(WriteR), .Q(register_3_q), .clk(Clock), .clr(Reset));
  Multiplexer #(.width(8), .enable("false")) multiplexer_1 (
    .in0(register_3_q), .in1({8{1'b0}}), .out(multiplexer_1_out), .sel(AluX));
  Multiplexer #(.width(8), .enable("false")) multiplexer_2 (
    .in0(ram_2_data), .in1({8{1'b0}}), .out(multiplexer_2_out), .sel(AluY));
  or or_1 (WriteR, decoder_1_out0, AluOp, AluX);
  or or_2 (WriteF, decoder_1_out0, AluOp);
  and and_2 (and_2_out, decoder_1_out5, FZ);
  and and_3 (and_3_out, decoder_1_out6, FC);
  // Probe on multiplexer_1_out
  // Probe on multiplexer_1_out
  // Probe on multiplexer_1_out
  // Probe on multiplexer_2_out
  // Probe on multiplexer_2_out
  // Probe on multiplexer_2_out
  or or_3 (JMP, decoder_1_out4, and_2_out, and_3_out);
  // Probe on sumador_restador_con_flags_1_resultado
  // Probe on sumador_restador_con_flags_1_resultado
  // Probe on sumador_restador_con_flags_1_resultado
  Sumador_Restador_con_flags sumador_restador_con_flags_1 (
    .Op(AluOp), .A(multiplexer_1_out), .B(multiplexer_2_out), .Acarreo__Carry(C), .Cero__Zero(Z),
    .Resultado(sumador_restador_con_flags_1_resultado));
  RAM #(.addrWidth(5), .bus("separate")) ram_2 (
    .addr(ram_1_data[4:0]), .din(sumador_restador_con_flags_1_resultado), .data(ram_2_data), .str(AluY),
    .clk(Clock));  // open: sel, ld, clr

  // Other names for the same wires on the sheet: WriteMD = AluY

  // Notes on the sheet:
  //   Tipo
  //   Procesamiento de datos
  //   Transferencia
  //   Control de flujo
  //   PC =  PC + 1
  //   Set de instrucciones
  //   Load
  //   Sintaxis
  //   ADD [dirección]
  //   SUB [dirección]
  //   LDA [dirección]
  //   STA [dirección]
  //   JMP dirección
  //   JZ    dirección
  //   JC    dirección
  //   HLT
  //   PC
  //   0
  //   1
  //   2
  //   3
  //   7. Detiene CPU (HLT)
  //   CodeOp
  //   000
  //   0 =
  //   001
  //   1 =
  //   2 =
  //   010
  //   3 =
  //   011
  //   4 =
  //   100
  //   5 =
  //   101
  //   6 =
  //   110
  //   7 =
  //   111
  //   Memoria de instrucciones
  //   Código.mem
  //   LDA [0]
  //   SUB [1]
  //   JZ 0
  //   HLT
  //   AluX
  //   0
  //   0
  //   1
  //   0
  //   0
  //   0
  //   0
  //   0
  //   Z
  //    = 0x40 hex
  //    = 0x21 hex
  //    = 0xA0 hex
  //    = 0xE0 hex
  //   ALUOp
  //   AluY
  //   0
  //   0
  //   1
  //   0
  //   0
  //   0
  //   0
  //   1
  //   0
  //   0
  //   0
  //   0
  //   0
  //   0
  //   0
  //   0
  //   C
  //   Dirección
  //   CodeOp
  //   Señales de control
  //   WriteMD
  //   WriteR
  //   1
  //   0
  //   1
  //   0
  //   1
  //   0
  //   0
  //   1
  //   0
  //   0
  //   0
  //   0
  //   0
  //   0
  //   0
  //   0
  //   JMP
  //   0
  //   0
  //   0
  //   0
  //   1
  //   1
  //   1
  //   0
  //   HLT
  //   WriteF
  //   0
  //   1
  //   1
  //   0
  //   0
  //   0
  //   0
  //   0
  //   0
  //   0
  //   0
  //   0
  //   0
  //   0
  //   0
  //   1
  //   AC
  //   Unidad de Control
  //   CodeOp
  //    Habilitación escritura registro AC
  //    Habilitación escritura registros Z y C
  //    Habilitación escritura Memoria de Datos
  //   Formato Instrucción
  //   Dirección
  //   | b7 b6 b5 | b4 b3 b2 b1 b0 | 
  //   (byte 1)
  //   datos.mem
  //   0x02 hex
  //   0
  //   0x03 hex
  //   1
  //   Memoria de datos
endmodule

module _8__Carga_inmediata__LDI (
  input  Clock
);

  wire AluOp, AluX, AluY, and_1_out, and_2_out, C, Contar, decoder_1_out0, decoder_1_out2, decoder_1_out4,
       decoder_1_out5, decoder_1_out6, FC, FZ, JMP, LDI, Reset, WriteF, WriteR, Z;
  wire [4:0] counter_1_q;
  wire [7:0] multiplexer_1_out, multiplexer_2_out, multiplexer_3_out, ram_1_data, ram_2_data, register_3_q,
       sumador_restador_con_flags_1_resultado;

  Button u_Reset (.out(Reset));
  Counter #(.width(5), .max('h1f)) counter_1 (
    .load(JMP), .D(ram_1_data[4:0]), .count(Contar), .Q(counter_1_q), .clk(Clock), .clr(Reset));  // open: carry
  nand nand_1 (Contar, JMP, 1'b1);
  // Probe on counter_1_q
  // Probe on counter_1_q
  Register #(.width(1)) register_1 (.D(Z), .en(WriteF), .Q(FZ), .clk(Clock));  // open: clr
  RAM #(.addrWidth(5)) ram_1 (.addr(counter_1_q), .data(ram_1_data));  // open: sel, clk, ld, clr
  // Probe on ram_1_data[4:0]
  // Probe on ram_1_data[4:0]
  // Probe on ram_1_data[7:5]
  // Probe on ram_1_data[7:5]
  Register #(.width(1)) register_2 (.D(C), .en(WriteF), .Q(FC), .clk(Clock));  // open: clr
  Decoder #(.select(3), .enable("false")) decoder_1 (
    .out0(decoder_1_out0), .out1(AluOp), .out2(decoder_1_out2), .out3(AluY), .out4(decoder_1_out4),
    .out5(decoder_1_out5), .out6(decoder_1_out6), .out7(LDI), .sel(ram_1_data[7:5]));
  Register register_3 (
    .D(sumador_restador_con_flags_1_resultado), .en(WriteR), .Q(register_3_q), .clk(Clock), .clr(Reset));
  Multiplexer #(.width(8), .enable("false")) multiplexer_1 (
    .in0(ram_2_data), .in1({3'b000, ram_1_data[4:0]}), .out(multiplexer_1_out), .sel(LDI));
  or or_1 (WriteR, decoder_1_out0, AluOp, decoder_1_out2, LDI);
  or or_2 (WriteF, decoder_1_out0, AluOp);
  or or_3 (AluX, decoder_1_out2, LDI);
  and and_1 (and_1_out, decoder_1_out5, FZ);
  and and_2 (and_2_out, decoder_1_out6, FC);
  Multiplexer #(.width(8), .enable("false")) multiplexer_2 (
    .in0(register_3_q), .in1({8{1'b0}}), .out(multiplexer_2_out), .sel(AluX));
  Multiplexer #(.width(8), .enable("false")) multiplexer_3 (
    .in0(multiplexer_1_out), .in1({8{1'b0}}), .out(multiplexer_3_out), .sel(AluY));
  or or_4 (JMP, decoder_1_out4, and_1_out, and_2_out);
  // Probe on multiplexer_2_out
  // Probe on multiplexer_2_out
  // Probe on multiplexer_2_out
  // Probe on multiplexer_3_out
  // Probe on multiplexer_3_out
  // Probe on multiplexer_3_out
  // Probe on sumador_restador_con_flags_1_resultado
  // Probe on sumador_restador_con_flags_1_resultado
  // Probe on sumador_restador_con_flags_1_resultado
  Sumador_Restador_con_flags sumador_restador_con_flags_1 (
    .Op(AluOp), .A(multiplexer_2_out), .B(multiplexer_3_out), .Acarreo__Carry(C), .Cero__Zero(Z),
    .Resultado(sumador_restador_con_flags_1_resultado));
  RAM #(.addrWidth(5), .bus("separate")) ram_2 (
    .addr(ram_1_data[4:0]), .din(sumador_restador_con_flags_1_resultado), .data(ram_2_data), .str(AluY),
    .clk(Clock));  // open: sel, ld, clr

  // Other names for the same wires on the sheet: WriteMD = AluY

  // Notes on the sheet:
  //   Tipo
  //   Procesamiento de datos
  //   Transferencia
  //   Control de flujo
  //   PC =  PC + 1
  //   Set de instrucciones
  //   Load
  //   Sintaxis
  //   ADD [dirección]
  //   SUB [dirección]
  //   LDA [dirección]
  //   STA [dirección]
  //   JMP dirección
  //   JZ    dirección
  //   JC    dirección
  //   LDI  valor
  //   PC
  //   CodeOp
  //   000
  //   0 =
  //   001
  //   1 =
  //   2 =
  //   010
  //   3 =
  //   011
  //   4 =
  //   100
  //   5 =
  //   101
  //   6 =
  //   110
  //   7 =
  //   111
  //   Memoria de instrucciones
  //   Código.mem
  //   LDI 3
  //   0
  //   SUB [1]
  //   1
  //   JZ 0
  //   2
  //   3
  //   HLT
  //   8. Carga inmediata (LDI)
  //   AluX
  //   0
  //   0
  //   1
  //   0
  //   0
  //   0
  //   0
  //   1
  //   Z
  //    = 0xE3 hex
  //    = 0x21 hex
  //    = 0xA0 hex
  //    = 0x83 hex
  //   ALUOp
  //   AluY
  //   0
  //   0
  //   1
  //   0
  //   0
  //   0
  //   1
  //   0
  //   0
  //   0
  //   0
  //   0
  //   0
  //   0
  //   0
  //   0
  //   C
  //   Dirección
  //   CodeOp
  //   Señales de control
  //   WriteR
  //   WriteMD
  //   1
  //   0
  //   1
  //   0
  //   1
  //   0
  //   0
  //   1
  //   0
  //   0
  //   0
  //   0
  //   0
  //   0
  //   1
  //   0
  //   JMP
  //   0
  //   0
  //   0
  //   0
  //   1
  //   1
  //   1
  //   0
  //   AC
  //   LDI
  //   WriteF
  //   0
  //   1
  //   1
  //   0
  //   0
  //   0
  //   0
  //   0
  //   0
  //   0
  //   0
  //   0
  //   0
  //   0
  //   0
  //   1
  //   Unidad de Control
  //   CodeOp
  //    Habilitación escritura registro AC
  //    Habilitación escritura registros Z y C
  //    Habilitación escritura Memoria de Datos
  //   Formato Instrucción
  //   Dirección
  //   | b7 b6 b5 | b4 b3 b2 b1 b0 | 
  //   (byte 1)
  //   HLT es un pseudo-instrucción que se codifica como JMP dirección. 
  //   donde dirección es igual a ubicación donde se encuentra la instrucción JMP.
  //   0
  //   1
  //   datos.mem
  //   0x02 hex
  //   0x03 hex
  //   Memoria de datos
endmodule
