// Logisim project Sim-AC-Neumann.circ as structural Verilog: 15 circuits, main circuit Sumador-Restador 4 bits
module Semisumador_1_bit (
  input  A,
  input  B,
  output Resultado,
  output Acarreo_out
);

  and and_1 (Acarreo_out, A, B);
  xor xor_1 (Resultado, A, B);

  // Notes on the sheet:
  //   Semisumador
  //   A
  //   B
  //   0
  //   0
  //   0
  //   1
  //   1
  //   0
  //   1
  //   1
  //   AND
  //   0
  //   0
  //   0
  //   1
  //   B
  //   A
  //   0
  //   0
  //   0
  //   0
  //   1
  //   0
  //   1
  //   0
  //   0
  //   1
  //   1
  //   1
  //   XOR
  //   A
  //   B
  //   0
  //   0
  //   0
  //   1
  //   0
  //   1
  //   1
  //   1
  //   0
  //   1
  //   1
  //   0
  //   Acarreo-out
  //   Resultado
  //   0
  //   1
  //   1
  //   0
  //   = 0
  //   = 1
  //   = 1
  //   = 2
endmodule

module Sumadorcompleto_1_bit (
  input  Acarreo_in,
  input  A,
  input  B,
  output Resultado,
  output Acarreo_out
);

  wire and_1_out, and_2_out, xor_1_out;

  and and_1 (and_1_out, A, B);
  xor xor_1 (xor_1_out, A, B);
  or or_1 (Acarreo_out, and_1_out, and_2_out);
  and and_2 (and_2_out, Acarreo_in, xor_1_out);
  xor xor_2 (Resultado, Acarreo_in, xor_1_out);

  // Notes on the sheet:
  //   Semisumador
  //   Sumador completo
  //   Semisumador
endmodule

module Sumador_Restador_4_bits (
  input  Op,
  input  [3:0] A,
  input  [3:0] B,
  output [3:0] Resultado,
  output Acarreo_out
);

  wire sumadorcompleto_1_bit_1_acarreo_out, sumadorcompleto_1_bit_2_acarreo_out,
       sumadorcompleto_1_bit_3_acarreo_out, xor_1_out, xor_2_out, xor_3_out, xor_4_out;

  // Probe on A
  // Probe on B
  // Probe on A
  // Probe on B
  xor xor_1 (xor_1_out, Op, B[3]);
  xor xor_2 (xor_2_out, Op, B[2]);
  xor xor_3 (xor_3_out, Op, B[1]);
  xor xor_4 (xor_4_out, Op, B[0]);
  Sumadorcompleto_1_bit sumadorcompleto_1_bit_1 (
    .A(A[0]), .B(xor_4_out), .Resultado(Resultado[0]), .Acarreo_out(sumadorcompleto_1_bit_1_acarreo_out),
    .Acarreo_in(Op));
  Sumadorcompleto_1_bit sumadorcompleto_1_bit_2 (
    .A(A[1]), .B(xor_3_out), .Resultado(Resultado[1]), .Acarreo_out(sumadorcompleto_1_bit_2_acarreo_out),
    .Acarreo_in(sumadorcompleto_1_bit_1_acarreo_out));
  Sumadorcompleto_1_bit sumadorcompleto_1_bit_3 (
    .A(A[2]), .B(xor_2_out), .Resultado(Resultado[2]), .Acarreo_out(sumadorcompleto_1_bit_3_acarreo_out),
    .Acarreo_in(sumadorcompleto_1_bit_2_acarreo_out));
  Sumadorcompleto_1_bit sumadorcompleto_1_bit_4 (
    .A(A[3]), .B(xor_1_out), .Resultado(Resultado[3]), .Acarreo_out(Acarreo_out),
    .Acarreo_in(sumadorcompleto_1_bit_3_acarreo_out));
  // Probe on Resultado
  // Probe on Resultado

  // Notes on the sheet:
  //   Acarreo-in
  //   0
  //   1
  //   Op
  //   Sumar
  //   Restar
endmodule

module Sumador_Restador_8_bits (
  input  Op,
  input  [7:0] A,
  input  [7:0] B,
  output [7:0] Resultado,
  output Acarreo_out
);

  wire sumadorcompleto_1_bit_1_acarreo_out, sumadorcompleto_1_bit_2_acarreo_out,
       sumadorcompleto_1_bit_3_acarreo_out, sumadorcompleto_1_bit_4_acarreo_out,
       sumadorcompleto_1_bit_5_acarreo_out, sumadorcompleto_1_bit_6_acarreo_out,
       sumadorcompleto_1_bit_7_acarreo_out, xor_1_out, xor_2_out, xor_3_out, xor_4_out, xor_5_out, xor_6_out,
       xor_7_out, xor_8_out;

  // Probe on A
  // Probe on B
  // Probe on A
  // Probe on B
  xor xor_1 (xor_1_out, Op, B[7]);
  xor xor_2 (xor_2_out, Op, B[6]);
  xor xor_3 (xor_3_out, Op, B[5]);
  xor xor_4 (xor_4_out, Op, B[4]);
  xor xor_5 (xor_5_out, Op, B[3]);
  xor xor_6 (xor_6_out, Op, B[2]);
  xor xor_7 (xor_7_out, Op, B[1]);
  xor xor_8 (xor_8_out, Op, B[0]);
  Sumadorcompleto_1_bit sumadorcompleto_1_bit_1 (
    .A(A[0]), .B(xor_8_out), .Resultado(Resultado[0]), .Acarreo_out(sumadorcompleto_1_bit_1_acarreo_out),
    .Acarreo_in(Op));
  Sumadorcompleto_1_bit sumadorcompleto_1_bit_2 (
    .A(A[1]), .B(xor_7_out), .Resultado(Resultado[1]), .Acarreo_out(sumadorcompleto_1_bit_2_acarreo_out),
    .Acarreo_in(sumadorcompleto_1_bit_1_acarreo_out));
  Sumadorcompleto_1_bit sumadorcompleto_1_bit_3 (
    .A(A[2]), .B(xor_6_out), .Resultado(Resultado[2]), .Acarreo_out(sumadorcompleto_1_bit_3_acarreo_out),
    .Acarreo_in(sumadorcompleto_1_bit_2_acarreo_out));
  Sumadorcompleto_1_bit sumadorcompleto_1_bit_4 (
    .A(A[3]), .B(xor_5_out), .Resultado(Resultado[3]), .Acarreo_out(sumadorcompleto_1_bit_4_acarreo_out),
    .Acarreo_in(sumadorcompleto_1_bit_3_acarreo_out));
  Sumadorcompleto_1_bit sumadorcompleto_1_bit_5 (
    .A(A[4]), .B(xor_4_out), .Resultado(Resultado[4]), .Acarreo_out(sumadorcompleto_1_bit_5_acarreo_out),
    .Acarreo_in(sumadorcompleto_1_bit_4_acarreo_out));
  Sumadorcompleto_1_bit sumadorcompleto_1_bit_6 (
    .A(A[5]), .B(xor_3_out), .Resultado(Resultado[5]), .Acarreo_out(sumadorcompleto_1_bit_6_acarreo_out),
    .Acarreo_in(sumadorcompleto_1_bit_5_acarreo_out));
  Sumadorcompleto_1_bit sumadorcompleto_1_bit_7 (
    .A(A[6]), .B(xor_2_out), .Resultado(Resultado[6]), .Acarreo_out(sumadorcompleto_1_bit_7_acarreo_out),
    .Acarreo_in(sumadorcompleto_1_bit_6_acarreo_out));
  Sumadorcompleto_1_bit sumadorcompleto_1_bit_8 (
    .A(A[7]), .B(xor_1_out), .Resultado(Resultado[7]), .Acarreo_out(Acarreo_out),
    .Acarreo_in(sumadorcompleto_1_bit_7_acarreo_out));
  // Probe on Resultado
  // Probe on Resultado

  // Notes on the sheet:
  //   Acarreo-in
  //   0
  //   1
  //   Op
  //   Sumar
  //   Restar
endmodule

module Sumador_Restador_con_flags (
  input  Op,
  input  [7:0] A,
  input  [7:0] B,
  output Acarreo__Carry,
  output Cero__Zero,
  output [7:0] Resultado
);

  wire A_Out, not_1_out, sumadorcompleto_1_bit_1_acarreo_out, sumadorcompleto_1_bit_2_acarreo_out,
       sumadorcompleto_1_bit_3_acarreo_out, sumadorcompleto_1_bit_4_acarreo_out,
       sumadorcompleto_1_bit_5_acarreo_out, sumadorcompleto_1_bit_6_acarreo_out,
       sumadorcompleto_1_bit_7_acarreo_out, xor_1_out, xor_2_out, xor_3_out, xor_4_out, xor_5_out, xor_6_out,
       xor_7_out, xor_8_out;

  // Probe on A
  // Probe on B
  // Probe on A
  // Probe on B
  xor xor_1 (xor_1_out, Op, B[7]);
  xor xor_2 (xor_2_out, Op, B[6]);
  xor xor_3 (xor_3_out, Op, B[5]);
  xor xor_4 (xor_4_out, Op, B[4]);
  xor xor_5 (xor_5_out, Op, B[3]);
  xor xor_6 (xor_6_out, Op, B[2]);
  xor xor_7 (xor_7_out, Op, B[1]);
  xor xor_8 (xor_8_out, Op, B[0]);
  Sumadorcompleto_1_bit sumadorcompleto_1_bit_1 (
    .A(A[0]), .B(xor_8_out), .Resultado(Resultado[0]), .Acarreo_out(sumadorcompleto_1_bit_1_acarreo_out),
    .Acarreo_in(Op));
  Sumadorcompleto_1_bit sumadorcompleto_1_bit_2 (
    .A(A[1]), .B(xor_7_out), .Resultado(Resultado[1]), .Acarreo_out(sumadorcompleto_1_bit_2_acarreo_out),
    .Acarreo_in(sumadorcompleto_1_bit_1_acarreo_out));
  Sumadorcompleto_1_bit sumadorcompleto_1_bit_3 (
    .A(A[2]), .B(xor_6_out), .Resultado(Resultado[2]), .Acarreo_out(sumadorcompleto_1_bit_3_acarreo_out),
    .Acarreo_in(sumadorcompleto_1_bit_2_acarreo_out));
  Sumadorcompleto_1_bit sumadorcompleto_1_bit_4 (
    .A(A[3]), .B(xor_5_out), .Resultado(Resultado[3]), .Acarreo_out(sumadorcompleto_1_bit_4_acarreo_out),
    .Acarreo_in(sumadorcompleto_1_bit_3_acarreo_out));
  Sumadorcompleto_1_bit sumadorcompleto_1_bit_5 (
    .A(A[4]), .B(xor_4_out), .Resultado(Resultado[4]), .Acarreo_out(sumadorcompleto_1_bit_5_acarreo_out),
    .Acarreo_in(sumadorcompleto_1_bit_4_acarreo_out));
  Sumadorcompleto_1_bit sumadorcompleto_1_bit_6 (
    .A(A[5]), .B(xor_3_out), .Resultado(Resultado[5]), .Acarreo_out(sumadorcompleto_1_bit_6_acarreo_out),
    .Acarreo_in(sumadorcompleto_1_bit_5_acarreo_out));
  Sumadorcompleto_1_bit sumadorcompleto_1_bit_7 (
    .A(A[6]), .B(xor_2_out), .Resultado(Resultado[6]), .Acarreo_out(sumadorcompleto_1_bit_7_acarreo_out),
    .Acarreo_in(sumadorcompleto_1_bit_6_acarreo_out));
  Sumadorcompleto_1_bit sumadorcompleto_1_bit_8 (
    .A(A[7]), .B(xor_1_out), .Resultado(Resultado[7]), .Acarreo_out(A_Out),
    .Acarreo_in(sumadorcompleto_1_bit_7_acarreo_out));
  not not_1 (not_1_out, A_Out);
  nor nor_1 (Cero__Zero, Resultado[0], Resultado[1], Resultado[2], Resultado[3], Resultado[4], Resultado[5], Resultado[6], Resultado[7]);
  // Probe on Resultado
  Multiplexer #(.enable("false")) multiplexer_1 (.in0(A_Out), .in1(not_1_out), .out(Acarreo__Carry), .sel(Op));
  // Probe on Resultado

  // Notes on the sheet:
  //   Acarreo-in
  //   0
  //   1
  //   Op
  //   Sumar
  //   Restar
  //   En la operación restar A+(-B) --> Acarreo =1, si A+(-B) está dentro del rango {0..255}
  //   Se cambia el comportamiento del Acarreo =1 en la operación restar --> Acerreo = 1, si A+(-B) < 0
  //   Para la operación +/- el acarreo = 1, si el resultado cae fuera del rango{0..255}
  //   En la operación sumar A+B --> Acarreo =1 si A+B > 255
  //   {0..255}
  //   Rango de valores enteros representables con 8 bits sin signo
  //   Entonces A<B porque A +(-B) <0 
  //   Funciona así:
  //   Si Acarreo (Carry) = 1:  A >= B
  //   Si Acarreo (Carry) = 0:  A < B 
  //   Pero queremos que funcione así:
  //   Si Acarreo (Carry) = 1:  A < B 
  //   A<B --> C=1
  //   Si Acarreo (Carry) = 0:  A >= B
endmodule

module _1__ALU__ADD_SUB (
  input  Clock,
  input  [7:0] Dato_desde_memoria,
  input  ALUOp
);

  wire [7:0] register_1_q, sumador_restador_8_bits_1_resultado;

  // Probe on sumador_restador_8_bits_1_resultado
  // Probe on sumador_restador_8_bits_1_resultado
  Register register_1 (.D(sumador_restador_8_bits_1_resultado), .Q(register_1_q), .clk(Clock));  // open: en, clr
  // Probe on sumador_restador_8_bits_1_resultado
  // Probe on register_1_q
  // Probe on register_1_q
  // Probe on register_1_q
  // Probe on Dato_desde_memoria
  // Probe on Dato_desde_memoria
  // Probe on Dato_desde_memoria
  Sumador_Restador_8_bits sumador_restador_8_bits_1 (
    .Op(ALUOp), .A(register_1_q), .B(Dato_desde_memoria), .Resultado(sumador_restador_8_bits_1_resultado));  // open: Acarreo_out

  // Notes on the sheet:
  //   Set de instrucciones
  //   Operaciones
  //   ADD
  //   SUB
  //   CodeOp
  //   0
  //   0
  //   0 =
  //   1 =
  //   1
  //   1
  //   ALUOp
  //   1. ALU (ADD-SUB)
  //   Registro
  //   Registro AC: ACumulador
  //   AC
  //   ALUOp
  //   AC: registro ACumulador se escribe por flanco ascendente o de subida, es decir cuando cambia de 0 a 1 el clock
endmodule

module _2__Cargar_de_memoria__LDA (
  input  Clock,
  input  [4:0] PC
);

  wire Contador_de_fase_q, Execute, Fetch;
  wire [4:0] multiplexer_1_out;
  wire [7:0] multiplexer_2_out, ram_1_data, register_1_q, register_2_q, sumador_restador_8_bits_1_resultado;

  // Probe on PC
  // Probe on PC
  // Probe on register_1_q[4:0]
  // Probe on register_1_q[4:0]
  Multiplexer #(.width(5), .enable("false")) multiplexer_1 (
    .in0(PC), .in1(register_1_q[4:0]), .out(multiplexer_1_out), .sel(Execute));
  Counter #(.width(1), .max('h1)) Contador_de_fase (
    .Q(Contador_de_fase_q), .clk(Clock));  // open: load, D, count, carry, clr
  Decoder #(.enable("false")) decoder_1 (.out0(Fetch), .out1(Execute), .sel(Contador_de_fase_q));
  RAM #(.addrWidth(5)) ram_1 (.addr(multiplexer_1_out), .data(ram_1_data));  // open: sel, clk, ld, clr
  Register register_1 (.D(ram_1_data), .en(Fetch), .Q(register_1_q), .clk(Clock));  // open: clr
  // Probe on register_1_q[7:5]
  // Probe on register_1_q[7:5]
  Register register_2 (
    .D(sumador_restador_8_bits_1_resultado), .en(Execute), .Q(register_2_q), .clk(Clock));  // open: clr
  // Probe on sumador_restador_8_bits_1_resultado
  // Probe on sumador_restador_8_bits_1_resultado
  // Probe on sumador_restador_8_bits_1_resultado
  Multiplexer #(.width(8), .enable("false")) multiplexer_2 (
    .in0(register_2_q), .in1({8{1'b0}}), .out(multiplexer_2_out), .sel(register_1_q[6]));
  // Probe on multiplexer_2_out
  // Probe on multiplexer_2_out
  // Probe on multiplexer_2_out
  // Probe on ram_1_data
  // Probe on ram_1_data
  // Probe on ram_1_data
  Sumador_Restador_8_bits sumador_restador_8_bits_1 (
    .Op(register_1_q[5]), .A(multiplexer_2_out), .B(ram_1_data),
    .Resultado(sumador_restador_8_bits_1_resultado));  // open: Acarreo_out

  // Notes on the sheet:
  //   Set de instrucciones
  //   Sintaxis
  //   ADD [dirección]
  //   SUB [dirección]
  //   LDA [dirección]
  //   La [dirección] es una posición de la memoria de datos
  //   LDA [dirección] = LOAD ACCUMULATOR
  //   CodeOp
  //   000
  //   0 =
  //   1 =
  //   001
  //   2 =
  //   010
  //   2. Cargar de memoria (LDA)
  //   Señales de control
  //   AluX
  //   ALUOp
  //   0
  //   0
  //   0
  //   1
  //   1
  //   0
  //   LDA [4]
  //   0
  //   ADD [5]
  //   1
  //   LDA [6]
  //   2
  //   SUB [7]
  //   3
  //   = 0x02 hex
  //   4
  //   = 0x03 hex
  //   5
  //   = 0x04 hex
  //   6
  //   = 0x01 hex
  //   7
  //   Memoria de instrucciones y datos
  //   Programa.mem
  //    = 0x44 hex
  //    = 0x05 hex
  //    = 0x46 hex
  //    = 0x27 hex
  //   Formato Instrucción
  //   CodeOp
  //   | b7 b6  b5 | b4 b3 b2 b1 b0 | 
  //   (byte 1)
  //   Dirección
  //   Fase 1 => Captar instrucción
  //   Fase 2 => Ejecutar instrucción
  //   IR
  //   !!Cantidad de posiciones direccionables 2**5 = 32 posiciones
  //   AC
  //   CodeOp
  //   AluX
  //   Arquitectura Von Neumann
  //   Memoria de datos e intrucciones juntas
  //   ALUOp
endmodule

module _3__Registro_Program_Counter__PC (
  input  Clock
);

  wire AluOp, AluX, Contador_de_fase_q, Execute, Fetch, Reset;
  wire [4:0] adder_1_out, multiplexer_1_out, register_1_q, register_2_q;
  wire [7:0] multiplexer_2_out, ram_1_data, register_3_q, sumador_restador_8_bits_1_resultado;
  wire [7:5] register_2_q_2;

  Button u_Reset (.out(Reset));
  // Probe on register_1_q
  // Probe on adder_1_out
  Adder #(.width(5)) adder_1 (.a(register_1_q), .b(5'b00001), .out(adder_1_out));  // open: cin, cout
  Register #(.width(5)) register_1 (.D(adder_1_out), .en(Fetch), .Q(register_1_q), .clk(Clock), .clr(Reset));
  Counter #(.width(1), .max('h1)) Contador_de_fase (
    .Q(Contador_de_fase_q), .clk(Clock));  // open: load, D, count, carry, clr
  // Probe on register_1_q
  // Probe on register_1_q
  Decoder #(.enable("false")) decoder_1 (.out0(Fetch), .out1(Execute), .sel(Contador_de_fase_q));
  // Probe on register_2_q
  // Probe on register_2_q
  Multiplexer #(.width(5), .enable("false")) multiplexer_1 (
    .in0(register_1_q), .in1(register_2_q), .out(multiplexer_1_out), .sel(Execute));
  RAM #(.addrWidth(5)) ram_1 (.addr(multiplexer_1_out), .data(ram_1_data));  // open: sel, clk, ld, clr
  Register register_2 (.D(ram_1_data), .en(Fetch), .Q({register_2_q_2, register_2_q}), .clk(Clock), .clr(Reset));
  // Probe on register_2_q_2
  // Probe on register_2_q_2
  Decoder #(.select(3), .disabled(0), .enable("false")) decoder_2 (
    .out1(AluOp), .out2(AluX), .sel(register_2_q_2));  // open: out0, out3, out4, out5, out6, out7
  Register register_3 (
    .D(sumador_restador_8_bits_1_resultado), .en(Execute), .Q(register_3_q), .clk(Clock), .clr(Reset));
  // Probe on sumador_restador_8_bits_1_resultado
  // Probe on sumador_restador_8_bits_1_resultado
  // Probe on sumador_restador_8_bits_1_resultado
  Multiplexer #(.width(8), .enable("false")) multiplexer_2 (
    .in0(register_3_q), .in1({8{1'b0}}), .out(multiplexer_2_out), .sel(AluX));
  // Probe on multiplexer_2_out
  // Probe on multiplexer_2_out
  // Probe on multiplexer_2_out
  // Probe on ram_1_data
  // Probe on ram_1_data
  // Probe on ram_1_data
  Sumador_Restador_8_bits sumador_restador_8_bits_1 (
    .Op(AluOp), .A(multiplexer_2_out), .B(ram_1_data), .Resultado(sumador_restador_8_bits_1_resultado));  // open: Acarreo_out

  // Notes on the sheet:
  //   Sintaxis
  //   Registro PC =
  //   Set de instrucciones
  //   ADD [dirección]
  //   SUB [dirección]
  //   LDA [dirección]
  //   Program Counter
  //    PC + 1
  //   0 =
  //   1 =
  //   2 =
  //    El registro PC  se escribe por flanco ascendente o de subida (rising edge)
  //   CodeOp
  //   000
  //   001
  //   010
  //   PC
  //   El  PC se incrementa en la etapa de captación
  //   3. Registro Program Counter (PC)
  //   Señales de control
  //   AluX
  //   ALUOp
  //   0
  //   0
  //   0
  //   1
  //   1
  //   0
  //   0
  //   1
  //   2
  //   3
  //   4
  //   5
  //   6
  //   7
  //   CodeOp
  //   Memoria de instrucciones y datos
  //   Programa.mem
  //   LDA [4]
  //   ADD [5]
  //   LDA [6]
  //   SUB [7]
  //   = 0x02 hex
  //   = 0x03 hex
  //   = 0x04 hex
  //   = 0x01 hex
  //   Formato Instrucción
  //   Dirección
  //   | b7 b6  b5 | b4 b3 b2 b1 b0 | 
  //   Fase 1 => Captar instrucción
  //   Fase 2 => Ejecutar instrucción
  //    = 0x44 hex
  //    = 0x05 hex
  //    = 0x46 hex
  //    = 0x27 hex
  //   (byte 1)
  //   IR
  //   CodeOp
  //   AC
  //   Unidad de Control
endmodule

module _4_1__Almacenar_en_memoria__STA (
  input  Clock
);

  wire AluOp, AluX, Contador_de_fase_q, decoder_2_out0, decoder_2_out3, Execute, Fetch, or_1_out, Reset,
       WriteM, WriteR;
  wire [4:0] adder_1_out, multiplexer_1_out, register_1_q, register_2_q;
  wire [7:0] multiplexer_2_out, ram_1_data, register_3_q, sumador_restador_8_bits_1_resultado;
  wire [7:5] register_2_q_2;

  Button u_Reset (.out(Reset));
  // Probe on register_1_q
  // Probe on adder_1_out
  Adder #(.width(5)) adder_1 (.a(register_1_q), .b(5'b00001), .out(adder_1_out));  // open: cin, cout
  Register #(.width(5)) register_1 (.D(adder_1_out), .en(Fetch), .Q(register_1_q), .clk(Clock), .clr(Reset));
  Counter #(.width(1), .max('h1)) Contador_de_fase (
    .Q(Contador_de_fase_q), .clk(Clock));  // open: load, D, count, carry, clr
  // Probe on register_1_q
  // Probe on register_1_q
  Decoder #(.enable("false")) decoder_1 (.out0(Fetch), .out1(Execute), .sel(Contador_de_fase_q));
  // Probe on register_2_q
  // Probe on register_2_q
  Multiplexer #(.width(5), .enable("false")) multiplexer_1 (
    .in0(register_1_q), .in1(register_2_q), .out(multiplexer_1_out), .sel(Execute));
  RAM #(.addrWidth(5), .bus("separate")) ram_1 (
    .addr(multiplexer_1_out), .din(register_3_q), .data(ram_1_data), .str(WriteM), .clk(Clock));  // open: sel, ld, clr
  Register register_2 (.D(ram_1_data), .en(Fetch), .Q({register_2_q_2, register_2_q}), .clk(Clock), .clr(Reset));
  // Probe on register_2_q_2
  // Probe on register_2_q_2
  Decoder #(.select(3), .disabled(0), .enable("false")) decoder_2 (
    .out0(decoder_2_out0), .out1(AluOp), .out2(AluX), .out3(decoder_2_out3), .sel(register_2_q_2));  // open: out4, out5, out6, out7
  Register register_3 (
    .D(sumador_restador_8_bits_1_resultado), .en(WriteR), .Q(register_3_q), .clk(Clock), .clr(Reset));
  // Probe on sumador_restador_8_bits_1_resultado
  // Probe on sumador_restador_8_bits_1_resultado
  // Probe on sumador_restador_8_bits_1_resultado
  Multiplexer #(.width(8), .enable("false")) multiplexer_2 (
    .in0(register_3_q), .in1({8{1'b0}}), .out(multiplexer_2_out), .sel(AluX));
  or or_1 (or_1_out, decoder_2_out0, AluOp, AluX);
  // Probe on multiplexer_2_out
  // Probe on multiplexer_2_out
  // Probe on multiplexer_2_out
  // Probe on ram_1_data
  // Probe on ram_1_data
  // Probe on ram_1_data
  and and_1 (WriteR, or_1_out, Execute);
  and and_2 (WriteM, Execute, decoder_2_out3);
  Sumador_Restador_8_bits sumador_restador_8_bits_1 (
    .Op(AluOp), .A(multiplexer_2_out), .B(ram_1_data), .Resultado(sumador_restador_8_bits_1_resultado));  // open: Acarreo_out

  // Notes on the sheet:
  //   Sintaxis
  //    PC + 1
  //   Set de instrucciones
  //   ADD [dirección]
  //   SUB [dirección]
  //   LDA [dirección]
  //   STA [dirección]
  //   CodeOp
  //   0 =
  //   1 =
  //   2 =
  //   3 =
  //   STA [dirección] = STORE ACCUMULATOR
  //   PC
  //   AluX
  //   0
  //   000
  //   0
  //   001
  //   1
  //   010
  //   0
  //   011
  //   Dirección
  //   4.1. Almacenar en memoria (STA)
  //   ALUOp
  //   0
  //   1
  //   0
  //   0
  //   Señales de control
  //   WriteR
  //   WriteMD
  //   1
  //   0
  //   1
  //   0
  //   1
  //   0
  //   0
  //   1
  //   Memoria de instrucciones y datos
  //   Programa.mem
  //   LDA [4]
  //   0
  //   ADD [5]
  //   1
  //   STA [6]
  //   2
  //   SUB [7]
  //   3
  //   = 0x02 hex
  //   4
  //   = 0x03 hex
  //   5
  //   = 0x04 hex
  //   6
  //   = 0x01 hex
  //   7
  //    = 0x44 hex
  //    = 0x05 hex
  //    = 0x66 hex
  //    = 0x27 hex
  //   Formato Instrucción
  //   CodeOp
  //   | b7 b6  b5 | b4 b3 b2 b1 b0 | 
  //   IR
  //   Dirección
  //   CodeOp
  //   (byte 1)
  //   AC
  //   Unidad de Control
  //    Habilitación escritura registro AC
  //    Habilitación escritura en memoria
endmodule

module _4_2__Almacenar_en_memoria__STA (
  input  Clock
);

  wire AluOp, AluX, Contador_de_fase_q, decoder_2_out0, decoder_2_out3, Execute, Fetch, or_1_out, Reset,
       WriteM, WriteR;
  wire [4:0] counter_1_q, multiplexer_1_out, register_1_q;
  wire [7:0] multiplexer_2_out, ram_1_data, register_2_q, sumador_restador_8_bits_1_resultado;
  wire [7:5] register_1_q_2;

  Button u_Reset (.out(Reset));
  Counter #(.width(5), .max('h1f)) counter_1 (
    .count(Fetch), .Q(counter_1_q), .clk(Clock), .clr(Reset));  // open: load, D, carry
  // Probe on counter_1_q
  // Probe on counter_1_q
  Counter #(.width(1), .max('h1)) Contador_de_fase (
    .Q(Contador_de_fase_q), .clk(Clock));  // open: load, D, count, carry, clr
  Decoder #(.enable("false")) decoder_1 (.out0(Fetch), .out1(Execute), .sel(Contador_de_fase_q));
  // Probe on register_1_q
  // Probe on register_1_q
  Multiplexer #(.width(5), .enable("false")) multiplexer_1 (
    .in0(counter_1_q), .in1(register_1_q), .out(multiplexer_1_out), .sel(Execute));
  RAM #(.addrWidth(5), .bus("separate")) ram_1 (
    .addr(multiplexer_1_out), .din(register_2_q), .data(ram_1_data), .str(WriteM), .clk(Clock));  // open: sel, ld, clr
  Register register_1 (.D(ram_1_data), .en(Fetch), .Q({register_1_q_2, register_1_q}), .clk(Clock), .clr(Reset));
  // Probe on register_1_q_2
  // Probe on register_1_q_2
  Decoder #(.select(3), .disabled(0), .enable("false")) decoder_2 (
    .out0(decoder_2_out0), .out1(AluOp), .out2(AluX), .out3(decoder_2_out3), .sel(register_1_q_2));  // open: out4, out5, out6, out7
  Register register_2 (
    .D(sumador_restador_8_bits_1_resultado), .en(WriteR), .Q(register_2_q), .clk(Clock), .clr(Reset));
  // Probe on sumador_restador_8_bits_1_resultado
  // Probe on sumador_restador_8_bits_1_resultado
  // Probe on sumador_restador_8_bits_1_resultado
  Multiplexer #(.width(8), .enable("false")) multiplexer_2 (
    .in0(register_2_q), .in1({8{1'b0}}), .out(multiplexer_2_out), .sel(AluX));
  or or_1 (or_1_out, decoder_2_out0, AluOp, AluX);
  // Probe on multiplexer_2_out
  // Probe on multiplexer_2_out
  // Probe on multiplexer_2_out
  // Probe on ram_1_data
  // Probe on ram_1_data
  // Probe on ram_1_data
  and and_1 (WriteR, or_1_out, Execute);
  and and_2 (WriteM, Execute, decoder_2_out3);
  Sumador_Restador_8_bits sumador_restador_8_bits_1 (
    .Op(AluOp), .A(multiplexer_2_out), .B(ram_1_data), .Resultado(sumador_restador_8_bits_1_resultado));  // open: Acarreo_out

  // Notes on the sheet:
  //   Tipo
  //   Procesamiento de datos
  //   Transferencia
  //   Si ct =1 y clock =1 --> PC =  PC + 1 
  //   Set de instrucciones
  //   !!Se organiza las instrucciones por tipo
  //   PC
  //   Funciona con flanco de subida cuando el clock pasa de 0 a 1
  //   Sintaxis
  //   ADD [dirección]
  //   SUB [dirección]
  //   LDA [dirección]
  //   STA [dirección]
  //   Dirección
  //   4.2. Almacenar en memoria (STA)
  //   LDA [4]
  //   0
  //   ADD [5]
  //   1
  //   STA [6]
  //   2
  //   SUB [7]
  //   3
  //   4
  //   5
  //   6
  //   7
  //   CodeOp
  //   000
  //   0 =
  //   1 =
  //   001
  //   2 =
  //   010
  //   3 =
  //   011
  //   Memoria de instrucciones y datos
  //   Programa.mem
  //    = 0x44 hex
  //    = 0x05 hex
  //    = 0x66 hex
  //    = 0x27 hex
  //   = 0x02 hex
  //   = 0x03 hex
  //   = 0x04 hex
  //   = 0x01 hex
  //   AluX
  //   ALUOp
  //   0
  //   0
  //   1
  //   0
  //   0
  //   0
  //   Señales de control
  //   WriteR
  //   0
  //   1
  //   1
  //   1
  //   1
  //   0
  //   WriteMD
  //   0
  //   0
  //   0
  //   1
  //   IR
  //   CodeOp
  //   CodeOp
  //   AC
  //   Formato Instrucción
  //   Dirección
  //   | b7 b6  b5 | b4 b3 b2 b1 b0 | 
  //   Unidad de Control
  //   (byte 1)
  //    Habilitación escritura registro AC
  //    Habilitación escritura en memoria
endmodule

module _5__Salto_incondiconal__JMP (
  input  Clock
);

  wire AluOp, AluX, Contador_de_fase_q, decoder_2_out0, decoder_2_out3, decoder_2_out4, Execute, Fetch, JMP,
       or_1_out, Reset, WriteM, WriteR;
  wire [4:0] counter_1_q, multiplexer_1_out, register_1_q;
  wire [7:0] multiplexer_2_out, ram_1_data, register_2_q, sumador_restador_8_bits_1_resultado;
  wire [7:5] register_1_q_2;

  Button u_Reset (.out(Reset));
  Counter #(.width(5), .max('h1f)) counter_1 (
    .load(JMP), .D(register_1_q), .count(Fetch), .Q(counter_1_q), .clk(Clock), .clr(Reset));  // open: carry
  // Probe on counter_1_q
  // Probe on counter_1_q
  Counter #(.width(1), .max('h1)) Contador_de_fase (
    .Q(Contador_de_fase_q), .clk(Clock));  // open: load, D, count, carry, clr
  Decoder #(.enable("false")) decoder_1 (.out0(Fetch), .out1(Execute), .sel(Contador_de_fase_q));
  // Probe on register_1_q
  // Probe on register_1_q
  Multiplexer #(.width(5), .enable("false")) multiplexer_1 (
    .in0(counter_1_q), .in1(register_1_q), .out(multiplexer_1_out), .sel(Execute));
  RAM #(.addrWidth(5), .bus("separate")) ram_1 (
    .addr(multiplexer_1_out), .din(register_2_q), .data(ram_1_data), .str(WriteM), .clk(Clock));  // open: sel, ld, clr
  Register register_1 (.D(ram_1_data), .en(Fetch), .Q({register_1_q_2, register_1_q}), .clk(Clock), .clr(Reset));
  // Probe on register_1_q_2
  // Probe on register_1_q_2
  Decoder #(.select(3), .disabled(0), .enable("false")) decoder_2 (
    .out0(decoder_2_out0), .out1(AluOp), .out2(AluX), .out3(decoder_2_out3), .out4(decoder_2_out4),
    .sel(register_1_q_2));  // open: out5, out6, out7
  Register register_2 (
    .D(sumador_restador_8_bits_1_resultado), .en(WriteR), .Q(register_2_q), .clk(Clock), .clr(Reset));
  // Probe on sumador_restador_8_bits_1_resultado
  // Probe on sumador_restador_8_bits_1_resultado
  // Probe on sumador_restador_8_bits_1_resultado
  Multiplexer #(.width(8), .enable("false")) multiplexer_2 (
    .in0(register_2_q), .in1({8{1'b0}}), .out(multiplexer_2_out), .sel(AluX));
  or or_1 (or_1_out, decoder_2_out0, AluOp, AluX);
  // Probe on multiplexer_2_out
  // Probe on multiplexer_2_out
  // Probe on multiplexer_2_out
  // Probe on ram_1_data
  // Probe on ram_1_data
  // Probe on ram_1_data
  and and_1 (WriteR, or_1_out, Execute);
  and and_2 (WriteM, Execute, decoder_2_out3);
  and and_3 (JMP, Execute, decoder_2_out4);
  Sumador_Restador_8_bits sumador_restador_8_bits_1 (
    .Op(AluOp), .A(multiplexer_2_out), .B(ram_1_data), .Resultado(sumador_restador_8_bits_1_resultado));  // open: Acarreo_out

  // Notes on the sheet:
  //   Tipo
  //   Procesamiento de datos
  //   Transferencia
  //   Control de flujo
  //   Load
  //   Set de instrucciones
  //   PC
  //   Sintaxis
  //   ADD [dirección]
  //   SUB [dirección]
  //   LDA [dirección]
  //   STA [dirección]
  //   JMP dirección
  //   Dirección
  //   En las instrucciones de control de flujo la [dirección] es una posición de la memoria de instrucciones
  //   LDA [4]
  //   0
  //   JMP 3
  //   1
  //   STA [5]
  //   2
  //   JMP 0
  //   3
  //   4
  //   5
  //   6.1. Saltos Incondicional(JMP)
  //   CodeOp
  //   000
  //   0 =
  //   001
  //   1 =
  //   2 =
  //   010
  //   3 =
  //   011
  //   4 =
  //   100
  //   Memoria de instrucciones y datos
  //   Programa.mem
  //    = 0x44 hex
  //    = 0x83 hex
  //    = 0x65 hex
  //    = 0x80 hex
  //   = 0x02 hex
  //   = 0x03 hex
  //   AluX
  //   0
  //   0
  //   1
  //   0
  //   0
  //   ALUOp
  //   WriteR
  //   0
  //   1
  //   1
  //   1
  //   0
  //   1
  //   0
  //   0
  //   0
  //   0
  //   Señales de control
  //   WriteMD
  //   0
  //   0
  //   0
  //   1
  //   0
  //   IR
  //   JMP
  //   0
  //   0
  //   0
  //   1
  //   1
  //   CodeOp
  //   AC
  //   Formato Instrucción
  //   CodeOp
  //   Unidad de Control
  //   Dirección
  //   | b7 b6 b5 | b4 b3 b2 b1 b0 | 
  //   (byte 1)
  //    Habilitación escritura registro AC
  //    Habilitación escritura en memoria
endmodule

module _6_1__Saltos_condicionales__JZ (
  input  Clock
);

  wire AluOp, AluX, and_1_out, Contador_de_fase_q, decoder_2_out0, decoder_2_out3, decoder_2_out4,
       decoder_2_out5, Execute, Fetch, FZ, JMP, or_1_out, or_2_out, or_3_out, Reset, WriteF, WriteM, WriteR,
       Z;
  wire [4:0] counter_1_q, multiplexer_1_out;
  wire [7:0] multiplexer_2_out, ram_1_data, register_2_q, register_3_q,
       sumador_restador_con_flags_1_resultado;

  Button u_Reset (.out(Reset));
  Counter #(.width(5), .max('h1f)) counter_1 (
    .load(JMP), .D(register_2_q[4:0]), .count(Fetch), .Q(counter_1_q), .clk(Clock), .clr(Reset));  // open: carry
  // Probe on counter_1_q
  // Probe on counter_1_q
  Counter #(.width(1), .max('h1)) Contador_de_fase (
    .Q(Contador_de_fase_q), .clk(Clock));  // open: load, D, count, carry, clr
  Decoder #(.enable("false")) decoder_1 (.out0(Fetch), .out1(Execute), .sel(Contador_de_fase_q));
  // Probe on register_2_q[4:0]
  // Probe on register_2_q[4:0]
  Multiplexer #(.width(5), .enable("false")) multiplexer_1 (
    .in0(counter_1_q), .in1(register_2_q[4:0]), .out(multiplexer_1_out), .sel(Execute));
  RAM #(.addrWidth(5), .bus("separate")) ram_1 (
    .addr(multiplexer_1_out), .din(register_3_q), .data(ram_1_data), .str(WriteM), .clk(Clock));  // open: sel, ld, clr
  Register #(.width(1)) register_1 (.D(Z), .en(WriteF), .Q(FZ), .clk(Clock), .clr(Reset));
  Register register_2 (.D(ram_1_data), .en(Fetch), .Q(register_2_q), .clk(Clock), .clr(Reset));
  // Probe on register_2_q[7:5]
  // Probe on register_2_q[7:5]
  Decoder #(.select(3), .disabled(0), .enable("false")) decoder_2 (
    .out0(decoder_2_out0), .out1(AluOp), .out2(AluX), .out3(decoder_2_out3), .out4(decoder_2_out4),
    .out5(decoder_2_out5), .sel(register_2_q[7:5]));  // open: out6, out7
  Register register_3 (
    .D(sumador_restador_con_flags_1_resultado), .en(WriteR), .Q(register_3_q), .clk(Clock), .clr(Reset));
  // Probe on sumador_restador_con_flags_1_resultado
  // Probe on sumador_restador_con_flags_1_resultado
  // Probe on sumador_restador_con_flags_1_resultado
  Multiplexer #(.width(8), .enable("false")) multiplexer_2 (
    .in0(register_3_q), .in1({8{1'b0}}), .out(multiplexer_2_out), .sel(AluX));
  or or_1 (or_1_out, decoder_2_out0, AluOp, AluX);
  or or_2 (or_2_out, decoder_2_out4, and_1_out);
  and and_1 (and_1_out, decoder_2_out5, FZ);
  // Probe on multiplexer_2_out
  // Probe on multiplexer_2_out
  // Probe on multiplexer_2_out
  // Probe on ram_1_data
  // Probe on ram_1_data
  // Probe on ram_1_data
  or or_3 (or_3_out, decoder_2_out0, AluOp);
  and and_2 (WriteF, or_3_out, Execute);
  and and_3 (WriteR, or_1_out, Execute);
  and and_4 (WriteM, Execute, decoder_2_out3);
  and and_5 (JMP, Execute, or_2_out);
  Sumador_Restador_con_flags sumador_restador_con_flags_1 (
    .Op(AluOp), .A(multiplexer_2_out), .B(ram_1_data), .Cero__Zero(Z),
    .Resultado(sumador_restador_con_flags_1_resultado));  // open: Acarreo__Carry

  // Notes on the sheet:
  //   Tipo
  //   Procesamiento de datos
  //   Transferencia
  //   Control de flujo
  //   Load
  //   Set de instrucciones
  //   La instrucción JZ salta si el registro Z tiene valor 1
  //   PC
  //   Sintaxis
  //   ADD [dirección]
  //   SUB [dirección]
  //   LDA [dirección]
  //   STA [dirección]
  //   JMP dirección
  //   JZ    dirección
  //   Dirección
  //   0
  //   1
  //   2
  //   3
  //   4
  //   5
  //   6.1. Saltos condicionales (JZ)
  //   CodeOp
  //   000
  //   0 =
  //   001
  //   1 =
  //   2 =
  //   010
  //   3 =
  //   011
  //   4 =
  //   100
  //   5 =
  //   101
  //   Memoria de instrucciones y datos
  //   Programa.mem
  //   LDA [4]
  //   SUB [5]
  //   JZ 0
  //   JMP 0
  //   0x02 hex
  //   0x03 hex
  //   AluX
  //   0
  //   0
  //   1
  //   0
  //   0
  //   0
  //    = 0x44 hex
  //    = 0x25 hex
  //    = 0xA0 hex
  //    = 0x80 hex
  //   WriteR
  //   ALUOp
  //   0
  //   1
  //   1
  //   1
  //   0
  //   1
  //   0
  //   0
  //   0
  //   0
  //   0
  //   0
  //   Z
  //   Señales de control
  //   WriteMD
  //   0
  //   0
  //   0
  //   1
  //   0
  //   0
  //   IR
  //   JMP
  //   WriteF
  //   1
  //   0
  //   1
  //   0
  //   0
  //   0
  //   0
  //   1
  //   0
  //   1
  //   0
  //   1
  //   CodeOp
  //   AC
  //   Unidad de Control
  //   Formato Instrucción
  //   CodeOp
  //   Dirección
  //   | b7 b6 b5 | b4 b3 b2 b1 b0 | 
  //   Solo para las instrucciones de procesamiento de datos se escribe los registros Flags
  //   (byte 1)
  //    Habilitación escritura registro Z
  //    Habilitación escritura registro AC
  //    Habilitación escritura en memoria
endmodule

module _6_2__Saltos_condicionales__JC (
  input  Clock
);

  wire AluOp, AluX, and_1_out, and_2_out, C, Contador_de_fase_q, decoder_2_out0, decoder_2_out3,
       decoder_2_out4, decoder_2_out5, decoder_2_out6, Execute, FC, Fetch, FZ, JMP, or_1_out, or_2_out,
       or_3_out, Reset, WriteF, WriteM, WriteR, Z;
  wire [4:0] counter_1_q, multiplexer_1_out;
  wire [7:0] multiplexer_2_out, ram_1_data, register_2_q, register_4_q,
       sumador_restador_con_flags_1_resultado;

  Button u_Reset (.out(Reset));
  Counter #(.width(5), .max('h1f)) counter_1 (
    .load(JMP), .D(register_2_q[4:0]), .count(Fetch), .Q(counter_1_q), .clk(Clock), .clr(Reset));  // open: carry
  // Probe on counter_1_q
  // Probe on counter_1_q
  Counter #(.width(1), .max('h1)) Contador_de_fase (
    .Q(Contador_de_fase_q), .clk(Clock));  // open: load, D, count, carry, clr
  Decoder #(.enable("false")) decoder_1 (.out0(Fetch), .out1(Execute), .sel(Contador_de_fase_q));
  // Probe on register_2_q[4:0]
  // Probe on register_2_q[4:0]
  Multiplexer #(.width(5), .enable("false")) multiplexer_1 (
    .in0(counter_1_q), .in1(register_2_q[4:0]), .out(multiplexer_1_out), .sel(Execute));
  RAM #(.addrWidth(5), .bus("separate")) ram_1 (
    .addr(multiplexer_1_out), .din(register_4_q), .data(ram_1_data), .str(WriteM), .clk(Clock));  // open: sel, ld, clr
  Register #(.width(1)) register_1 (.D(Z), .en(WriteF), .Q(FZ), .clk(Clock));  // open: clr
  Register register_2 (.D(ram_1_data), .en(Fetch), .Q(register_2_q), .clk(Clock), .clr(Reset));
  Register #(.width(1)) register_3 (.D(C), .en(WriteF), .Q(FC), .clk(Clock));  // open: clr
  // Probe on register_2_q[7:5]
  // Probe on register_2_q[7:5]
  Decoder #(.select(3), .disabled(0), .enable("false")) decoder_2 (
    .out0(decoder_2_out0), .out1(AluOp), .out2(AluX), .out3(decoder_2_out3), .out4(decoder_2_out4),
    .out5(decoder_2_out5), .out6(decoder_2_out6), .sel(register_2_q[7:5]));  // open: out7
  Register register_4 (
    .D(sumador_restador_con_flags_1_resultado), .en(WriteR), .Q(register_4_q), .clk(Clock), .clr(Reset));
  and and_1 (and_1_out, decoder_2_out5, FZ);
  and and_2 (and_2_out, decoder_2_out6, FC);
  // Probe on sumador_restador_con_flags_1_resultado
  // Probe on sumador_restador_con_flags_1_resultado
  // Probe on sumador_restador_con_flags_1_resultado
  Multiplexer #(.width(8), .enable("false")) multiplexer_2 (
    .in0(register_4_q), .in1({8{1'b0}}), .out(multiplexer_2_out), .sel(AluX));
  or or_1 (or_1_out, decoder_2_out0, AluOp, AluX);
  or or_2 (or_2_out, decoder_2_out4, and_1_out, and_2_out);
  // Probe on multiplexer_2_out
  // Probe on multiplexer_2_out
  // Probe on multiplexer_2_out
  // Probe on ram_1_data
  // Probe on ram_1_data
  // Probe on ram_1_data
  or or_3 (or_3_out, decoder_2_out0, AluOp);
  and and_3 (WriteF, or_3_out, Execute);
  and and_4 (WriteR, or_1_out, Execute);
  and and_5 (WriteM, Execute, decoder_2_out3);
  and and_6 (JMP, Execute, or_2_out);
  Sumador_Restador_con_flags sumador_restador_con_flags_1 (
    .Op(AluOp), .A(multiplexer_2_out), .B(ram_1_data), .Acarreo__Carry(C), .Cero__Zero(Z),
    .Resultado(sumador_restador_con_flags_1_resultado));

  // Notes on the sheet:
  //   Tipo
  //   Procesamiento de datos
  //   Transferencia
  //   Control de flujo
  //   Load
  //   Set de instrucciones
  //   PC
  //   Sintaxis
  //   ADD [dirección]
  //   SUB [dirección]
  //   LDA [dirección]
  //   STA [dirección]
  //   JMP dirección
  //   JZ    dirección
  //   JC   dirección
  //   La instrucción JC salta si el registro C tiene valor 1 
  //   Dirección
  //   0
  //   1
  //   2
  //   3
  //   4
  //   5
  //   6.2. Saltos condicionales (JC)
  //   CodeOp
  //   000
  //   0 =
  //   001
  //   1 =
  //   2 =
  //   010
  //   3 =
  //   011
  //   4 =
  //   100
  //   5 =
  //   101
  //   6 =
  //   110
  //   Memoria de instrucciones y datos
  //   Programa.mem
  //   LDA [4]
  //   SUB [5]
  //   JC 0
  //   JMP 0
  //   0x02 hex
  //   0x03 hex
  //   AluX
  //   0
  //   0
  //   1
  //   0
  //   0
  //   0
  //   0
  //    = 0x44 hex
  //    = 0x25 hex
  //    = 0xC0 hex
  //    = 0x80 hex
  //   WriteR
  //   ALUOp
  //   0
  //   1
  //   1
  //   1
  //   0
  //   1
  //   0
  //   0
  //   0
  //   0
  //   0
  //   0
  //   0
  //   0
  //   Z
  //   Señales de control
  //   WriteMD
  //   0
  //   0
  //   0
  //   1
  //   0
  //   0
  //   0
  //   IR
  //   JMP
  //   WriteF
  //   1
  //   0
  //   1
  //   0
  //   0
  //   0
  //   0
  //   1
  //   0
  //   1
  //   0
  //   1
  //   0
  //   1
  //   C
  //   CodeOp
  //   AC
  //   Formato Instrucción
  //   CodeOp
  //   | b7 b6 b5 | b4 b3 b2 b1 b0 | 
  //   Unidad de Control
  //   (byte 1)
  //   Dirección
  //    Habilitación escritura registro Z
  //    Habilitación escritura registro AC
  //    Habilitación escritura en memoria
endmodule

module _7__Detiene_CPU__HLT (
  input  Clock
);

  wire AluOp, AluX, and_2_out, and_3_out, C, Clock_t, Contador_de_fase_q, decoder_2_out0, decoder_2_out3,
       decoder_2_out4, decoder_2_out5, decoder_2_out6, Execute, FC, Fetch, FZ, HLT, JMP, or_1_out, or_2_out,
       or_3_out, Reset, WriteF, WriteM, WriteR, Z;
  wire [4:0] counter_1_q, multiplexer_1_out, register_2_q;
  wire [7:0] multiplexer_2_out, ram_1_data, register_4_q, sumador_restador_con_flags_1_resultado;
  wire [7:5] register_2_q_2;

  Button u_Reset (.out(Reset));
  and and_1 (Clock_t, ~HLT, Clock);  // AND_Gate
  // Probe on counter_1_q
  // Probe on counter_1_q
  Counter #(.width(5), .max('h1f)) counter_1 (
    .load(JMP), .D(register_2_q), .count(Fetch), .Q(counter_1_q), .clk(Clock_t), .clr(Reset));  // open: carry
  Counter #(.width(1), .max('h1)) Contador_de_fase (
    .Q(Contador_de_fase_q), .clk(Clock_t));  // open: load, D, count, carry, clr
  Decoder #(.enable("false")) decoder_1 (.out0(Fetch), .out1(Execute), .sel(Contador_de_fase_q));
  // Probe on register_2_q
  // Probe on register_2_q
  Multiplexer #(.width(5), .enable("false")) multiplexer_1 (
    .in0(counter_1_q), .in1(register_2_q), .out(multiplexer_1_out), .sel(Execute));
  RAM #(.addrWidth(5), .bus("separate")) ram_1 (
    .addr(multiplexer_1_out), .din(register_4_q), .data(ram_1_data), .str(WriteM), .clk(Clock_t));  // open: sel, ld, clr
  Register #(.width(1)) register_1 (.D(Z), .en(WriteF), .Q(FZ), .clk(Clock_t));  // open: clr
  Register register_2 (.D(ram_1_data), .en(Fetch), .Q({register_2_q_2, register_2_q}), .clk(Clock_t), .clr(Reset));
  Register #(.width(1)) register_3 (.D(C), .en(WriteF), .Q(FC), .clk(Clock_t));  // open: clr
  // Probe on register_2_q_2
  // Probe on register_2_q_2
  Decoder #(.select(3), .disabled(0), .enable("false")) decoder_2 (
    .out0(decoder_2_out0), .out1(AluOp), .out2(AluX), .out3(decoder_2_out3), .out4(decoder_2_out4),
    .out5(decoder_2_out5), .out6(decoder_2_out6), .out7(HLT), .sel(register_2_q_2));
  Register register_4 (
    .D(sumador_restador_con_flags_1_resultado), .en(WriteR), .Q(register_4_q), .clk(Clock_t), .clr(Reset));
  and and_2 (and_2_out, decoder_2_out5, FZ);
  and and_3 (and_3_out, decoder_2_out6, FC);
  // Probe on sumador_restador_con_flags_1_resultado
  // Probe on sumador_restador_con_flags_1_resultado
  // Probe on sumador_restador_con_flags_1_resultado
  Multiplexer #(.width(8), .enable("false")) multiplexer_2 (
    .in0(register_4_q), .in1({8{1'b0}}), .out(multiplexer_2_out), .sel(AluX));
  or or_1 (or_1_out, decoder_2_out0, AluOp, AluX);
  or or_2 (or_2_out, decoder_2_out4, and_2_out, and_3_out);
  // Probe on multiplexer_2_out
  // Probe on multiplexer_2_out
  // Probe on multiplexer_2_out
  // Probe on ram_1_data
  // Probe on ram_1_data
  // Probe on ram_1_data
  or or_3 (or_3_out, decoder_2_out0, AluOp);
  and and_4 (WriteF, or_3_out, Execute);
  and and_5 (WriteR, or_1_out, Execute);
  and and_6 (WriteM, Execute, decoder_2_out3);
  and and_7 (JMP, Execute, or_2_out);
  Sumador_Restador_con_flags sumador_restador_con_flags_1 (
    .Op(AluOp), .A(multiplexer_2_out), .B(ram_1_data), .Acarreo__Carry(C), .Cero__Zero(Z),
    .Resultado(sumador_restador_con_flags_1_resultado));

  // Notes on the sheet:
  //   Tipo
  //   Procesamiento de datos
  //   Transferencia
  //   Control de flujo
  //   PC
  //   Load
  //   Set de instrucciones
  //   Sintaxis
  //   ADD [dirección]
  //   SUB [dirección]
  //   LDA [dirección]
  //   STA [dirección]
  //   JMP dirección
  //   JZ    dirección
  //   JC    dirección
  //   HLT
  //   Dirección
  //   0
  //   1
  //   2
  //   3
  //   4
  //   5
  //   7. Detiene CPU (HLT)
  //   CodeOp
  //   000
  //   0 =
  //   001
  //   1 =
  //   2 =
  //   010
  //   3 =
  //   011
  //   4 =
  //   100
  //   5 =
  //   101
  //   6 =
  //   110
  //   7 =
  //   111
  //   Memoria de instrucciones y datos
  //   Programa.mem
  //   LDA [4]
  //   SUB [5]
  //   JC 0
  //   HLT
  //   0x02 hex
  //   0x03 hex
  //   AluX
  //   0
  //   0
  //   1
  //   0
  //   0
  //   0
  //   0
  //   0
  //    = 0x44 hex
  //    = 0x25 hex
  //    = 0xC0 hex
  //    = 0xE0 hex
  //   ALUOp
  //   WriteR
  //   0
  //   1
  //   1
  //   1
  //   0
  //   1
  //   0
  //   0
  //   0
  //   0
  //   0
  //   0
  //   0
  //   0
  //   0
  //   0
  //   Z
  //   IR
  //   Señales de control
  //   WriteMD
  //   0
  //   0
  //   0
  //   1
  //   0
  //   0
  //   0
  //   0
  //   C
  //   WriteF
  //   JMP
  //   1
  //   0
  //   1
  //   0
  //   0
  //   0
  //   0
  //   1
  //   0
  //   1
  //   0
  //   1
  //   0
  //   1
  //   0
  //   0
  //   CodeOp
  //   HLT
  //   0
  //   0
  //   0
  //   0
  //   0
  //   0
  //   0
  //   1
  //   AC
  //   Unidad de Control
  //   CodeOp
  //   Formato Instrucción
  //   Dirección
  //   | b7 b6 b5 | b4 b3 b2 b1 b0 | 
  //   (byte 1)
  //    Habilitación escritura registro Z
  //    Habilitación escritura registro AC
  //    Habilitación escritura en memoria
endmodule

module _8__Carga_inmediata__LDI (
  input  Clock
);

  wire AluOp, AluX, and_1_out, and_2_out, C, Contador_de_fase_q, decoder_2_out0, decoder_2_out2,
       decoder_2_out3, decoder_2_out4, decoder_2_out5, decoder_2_out6, Execute, FC, Fetch, FZ, JMP, LDI,
       or_1_out, or_2_out, or_4_out, Reset, WriteF, WriteM, WriteR, Z;
  wire [4:0] counter_1_q, multiplexer_1_out, register_2_q_2;
  wire [7:0] multiplexer_2_out, multiplexer_3_out, ram_1_data, register_4_q,
       sumador_restador_con_flags_1_resultado;
  wire [7:5] register_2_q;

  Button u_Reset (.out(Reset));
  // Probe on counter_1_q
  // Probe on counter_1_q
  Counter #(.width(5), .max('h1f)) counter_1 (
    .load(JMP), .D(register_2_q_2), .count(Fetch), .Q(counter_1_q), .clk(Clock), .clr(Reset));  // open: carry
  Counter #(.width(1), .max('h1)) Contador_de_fase (
    .Q(Contador_de_fase_q), .clk(Clock));  // open: load, D, count, carry, clr
  Decoder #(.enable("false")) decoder_1 (.out0(Fetch), .out1(Execute), .sel(Contador_de_fase_q));
  // Probe on register_2_q_2
  // Probe on register_2_q_2
  Multiplexer #(.width(5), .enable("false")) multiplexer_1 (
    .in0(counter_1_q), .in1(register_2_q_2), .out(multiplexer_1_out), .sel(Execute));
  RAM #(.addrWidth(5), .bus("separate")) ram_1 (
    .addr(multiplexer_1_out), .din(register_4_q), .data(ram_1_data), .str(WriteM), .clk(Clock));  // open: sel, ld, clr
  Register #(.width(1)) register_1 (.D(Z), .en(WriteF), .Q(FZ), .clk(Clock));  // open: clr
  Register register_2 (.D(ram_1_data), .en(Fetch), .Q({register_2_q, register_2_q_2}), .clk(Clock), .clr(Reset));
  Register #(.width(1)) register_3 (.D(C), .en(WriteF), .Q(FC), .clk(Clock));  // open: clr
  // Probe on register_2_q
  // Probe on register_2_q
  Decoder #(.select(3), .disabled(0), .enable("false")) decoder_2 (
    .out0(decoder_2_out0), .out1(AluOp), .out2(decoder_2_out2), .out3(decoder_2_out3), .out4(decoder_2_out4),
    .out5(decoder_2_out5), .out6(decoder_2_out6), .out7(LDI), .sel(register_2_q));
  Register register_4 (
    .D(sumador_restador_con_flags_1_resultado), .en(WriteR), .Q(register_4_q), .clk(Clock), .clr(Reset));
  and and_1 (and_1_out, decoder_2_out5, FZ);
  and and_2 (and_2_out, decoder_2_out6, FC);
  // Probe on sumador_restador_con_flags_1_resultado
  // Probe on sumador_restador_con_flags_1_resultado
  // Probe on sumador_restador_con_flags_1_resultado
  Multiplexer #(.width(8), .enable("false")) multiplexer_2 (
    .in0(register_4_q), .in1({8{1'b0}}), .out(multiplexer_2_out), .sel(AluX));
  Multiplexer #(.width(8), .enable("false")) multiplexer_3 (
    .in0(ram_1_data), .in1({3'b000, register_2_q_2}), .out(multiplexer_3_out), .sel(LDI));
  or or_1 (or_1_out, decoder_2_out0, AluOp, decoder_2_out2, LDI);
  or or_2 (or_2_out, decoder_2_out4, and_1_out, and_2_out);
  // Probe on multiplexer_2_out
  // Probe on multiplexer_2_out
  // Probe on multiplexer_2_out
  // Probe on multiplexer_3_out
  // Probe on multiplexer_3_out
  // Probe on multiplexer_3_out
  or or_3 (AluX, decoder_2_out2, LDI);
  or or_4 (or_4_out, decoder_2_out0, AluOp);
  and and_3 (WriteF, or_4_out, Execute);
  and and_4 (WriteR, or_1_out, Execute);
  and and_5 (WriteM, Execute, decoder_2_out3);
  and and_6 (JMP, Execute, or_2_out);
  Sumador_Restador_con_flags sumador_restador_con_flags_1 (
    .Op(AluOp), .A(multiplexer_2_out), .B(multiplexer_3_out), .Acarreo__Carry(C), .Cero__Zero(Z),
    .Resultado(sumador_restador_con_flags_1_resultado));

  // Notes on the sheet:
  //   Tipo
  //   Procesamiento de datos
  //   Transferencia
  //   Control de flujo
  //   PC
  //   Load
  //   Set de instrucciones
  //   Sintaxis
  //   ADD [dirección]
  //   SUB [dirección]
  //   LDA [dirección]
  //   STA [dirección]
  //   JMP dirección
  //   JZ    dirección
  //   JC    dirección
  //   LDI  valor
  //   Dirección
  //   0
  //   1
  //   2
  //   3
  //   4
  //   5
  //   8. Carga inmediata (LDI)
  //   CodeOp
  //   000
  //   0 =
  //   001
  //   1 =
  //   2 =
  //   010
  //   3 =
  //   011
  //   4 =
  //   100
  //   5 =
  //   101
  //   6 =
  //   110
  //   7 =
  //   111
  //   Memoria de instrucciones y datos
  //   Programa.mem
  //   LDI 3
  //   SUB [5]
  //   JC 0
  //   JMP 0
  //   0x02 hex
  //   0x03 hex
  //   AluX
  //   0
  //   0
  //   1
  //   0
  //   0
  //   0
  //   0
  //   1
  //    = 0xE3 hex
  //    = 0x25 hex
  //    = 0xC0 hex
  //    = 0x80 hex
  //   WriteR
  //   ALUOp
  //   0
  //   1
  //   1
  //   1
  //   0
  //   1
  //   0
  //   0
  //   0
  //   0
  //   0
  //   0
  //   0
  //   0
  //   0
  //   1
  //   Z
  //   IR
  //   Señales de control
  //   WriteMD
  //   0
  //   0
  //   0
  //   1
  //   0
  //   0
  //   0
  //   0
  //   C
  //   WriteF
  //   JMP
  //   1
  //   0
  //   1
  //   0
  //   0
  //   0
  //   0
  //   1
  //   0
  //   1
  //   0
  //   1
  //   0
  //   1
  //   0
  //   0
  //   CodeOp
  //   LDI
  //   0
  //   0
  //   0
  //   0
  //   0
  //   0
  //   0
  //   1
  //   AC
  //   Unidad de Control
  //   CodeOp
  //   Formato Instrucción
  //   Dirección
  //   | b7 b6 b5 | b4 b3 b2 b1 b0 | 
  //   (byte 1)
  //   HLT es un pseudo-instrucción que se codifica como JMP dirección. 
  //   donde dirección es igual a ubicación donde se encuentra la instrucción JMP.
  //    Habilitación escritura registro Z
  //    Habilitación escritura registro AC
  //    Habilitación escritura en memoria
endmodule
